// Logisim project 6502_trans.circ as structural Verilog
module _6502 (
  input  in_1,
  input  in_2,
  input  in_3,
  input  in_4,
  input  in_5,
  input  [7:0] in_6
);

  wire _421, _710, _943, _1163, data_output_register_1__63, data_output_register_1__97,
       data_output_register_1__444, data_output_register_1__746, data_output_register_1__1088,
       data_output_register_1__1415, data_output_register_1__1453, data_output_register_1__1634,
       instruction_register_1_out_10, instruction_register_1_out_11, predecode_logic_1_out_12,
       predecode_logic_1_out_13, predecode_logic_1_out_14, predecode_logic_1_out_15,
       predecode_logic_1_out_16, predecode_logic_1_out_17, predecode_logic_1_out_18, predecode_logic_1_out_19;
  wire [7:0] adh_precharge_mosfets_1_out_2, databus_precharge_mosfets_1_out_2,
       databus_tristate_buffers_1__1005;

  Clock_Generation clock_generation_1 (._1171(in_1), ._1163(_1163), ._421(_421), ._710(_710), ._943(_943));
  Predecode_Logic predecode_logic_1 (
    .in_4(in_6[0]), .in_5(in_6[1]), .in_6(in_6[2]), .in_7(in_6[3]), .in_8(in_6[4]), .in_9(in_6[5]),
    .in_10(in_6[6]), .in_11(in_6[7]), ._1077(in_5), ._710(_710), ._724(in_3),
    .out_12(predecode_logic_1_out_12), .out_13(predecode_logic_1_out_13), .out_14(predecode_logic_1_out_14),
    .out_15(predecode_logic_1_out_15), .out_16(predecode_logic_1_out_16), .out_17(predecode_logic_1_out_17),
    .out_18(predecode_logic_1_out_18), .out_19(predecode_logic_1_out_19));
  Predecode_Register predecode_register_1 (
    .in_2(databus_tristate_buffers_1__1005[0]), .in_3(databus_tristate_buffers_1__1005[1]),
    .in_4(databus_tristate_buffers_1__1005[2]), .in_5(databus_tristate_buffers_1__1005[3]),
    .in_6(databus_tristate_buffers_1__1005[4]), .in_7(databus_tristate_buffers_1__1005[5]),
    .in_8(databus_tristate_buffers_1__1005[6]), .in_9(databus_tristate_buffers_1__1005[7]), ._943(_943));  // open: _758, _361, _955, _894, _369, _829, _1669, _1690
  Instruction_Register instruction_register_1 (
    .in_2(predecode_logic_1_out_12), .in_3(predecode_logic_1_out_13), .in_4(predecode_logic_1_out_14),
    .in_5(predecode_logic_1_out_15), .in_6(predecode_logic_1_out_16), .in_7(predecode_logic_1_out_17),
    .in_8(predecode_logic_1_out_18), .in_9(predecode_logic_1_out_19), .in_1(_943),
    .out_10(instruction_register_1_out_10), .out_11(instruction_register_1_out_11));  // open: out_12, out_13, out_14, out_15, out_16, out_17, out_18, out_19, out_20, out_21, out_22, out_23, out_24, out_25
  Databus_Tristate_Buffers databus_tristate_buffers_1 (
    ._97(data_output_register_1__97), ._746(data_output_register_1__746),
    ._1634(data_output_register_1__1634), ._444(data_output_register_1__444),
    ._1088(data_output_register_1__1088), ._1453(data_output_register_1__1453),
    ._1415(data_output_register_1__1415), ._63(data_output_register_1__63), ._353(1'b0),
    ._1005(databus_tristate_buffers_1__1005[0]), ._82(databus_tristate_buffers_1__1005[1]),
    ._945(databus_tristate_buffers_1__1005[2]), ._650(databus_tristate_buffers_1__1005[3]),
    ._1393(databus_tristate_buffers_1__1005[4]), ._175(databus_tristate_buffers_1__1005[5]),
    ._1591(databus_tristate_buffers_1__1005[6]), ._1349(databus_tristate_buffers_1__1005[7]));
  Data_Output_Register data_output_register_1 (
    ._1108(databus_precharge_mosfets_1_out_2[0]), ._991(databus_precharge_mosfets_1_out_2[1]),
    ._1473(databus_precharge_mosfets_1_out_2[2]), ._1302(databus_precharge_mosfets_1_out_2[3]),
    ._892(databus_precharge_mosfets_1_out_2[4]), ._1503(databus_precharge_mosfets_1_out_2[5]),
    ._833(databus_precharge_mosfets_1_out_2[6]), ._493(databus_precharge_mosfets_1_out_2[7]), ._710(_710),
    ._97(data_output_register_1__97), ._746(data_output_register_1__746),
    ._1634(data_output_register_1__1634), ._444(data_output_register_1__444),
    ._1088(data_output_register_1__1088), ._1453(data_output_register_1__1453),
    ._1415(data_output_register_1__1415), ._63(data_output_register_1__63));
  Databus_Precharge_Mosfets databus_precharge_mosfets_1 (
    ._943(_943), .out_2(databus_precharge_mosfets_1_out_2[0]), .out_3(databus_precharge_mosfets_1_out_2[1]),
    .out_4(databus_precharge_mosfets_1_out_2[2]), .out_5(databus_precharge_mosfets_1_out_2[3]),
    .out_6(databus_precharge_mosfets_1_out_2[4]), .out_7(databus_precharge_mosfets_1_out_2[5]),
    .out_8(databus_precharge_mosfets_1_out_2[6]), .out_9(databus_precharge_mosfets_1_out_2[7]));
  Input_Data_Latch input_data_latch_1 (
    .in_2(databus_tristate_buffers_1__1005[0]), .in_3(databus_tristate_buffers_1__1005[1]),
    .in_4(databus_tristate_buffers_1__1005[2]), .in_5(databus_tristate_buffers_1__1005[3]),
    .in_6(databus_tristate_buffers_1__1005[4]), .in_7(databus_tristate_buffers_1__1005[5]),
    .in_8(databus_tristate_buffers_1__1005[6]), .in_9(databus_tristate_buffers_1__1005[7]), ._943(_943));  // open: in_10, in_11, in_12
  ADH_Precharge_Mosfets adh_precharge_mosfets_1 (
    ._943(_943), .out_2(adh_precharge_mosfets_1_out_2[0]), .out_3(adh_precharge_mosfets_1_out_2[1]),
    .out_4(adh_precharge_mosfets_1_out_2[2]), .out_5(adh_precharge_mosfets_1_out_2[3]),
    .out_6(adh_precharge_mosfets_1_out_2[4]), .out_7(adh_precharge_mosfets_1_out_2[5]),
    .out_8(adh_precharge_mosfets_1_out_2[6]), .out_9(adh_precharge_mosfets_1_out_2[7]));
  ADH_Open_Drain_Mosfets adh_open_drain_mosfets_1 (
    .in_1(in_4), .in_2(in_2), .out_3(adh_precharge_mosfets_1_out_2[0]),
    .out_4(adh_precharge_mosfets_1_out_2[1]), .out_5(adh_precharge_mosfets_1_out_2[2]),
    .out_6(adh_precharge_mosfets_1_out_2[3]), .out_7(adh_precharge_mosfets_1_out_2[4]),
    .out_8(adh_precharge_mosfets_1_out_2[5]), .out_9(adh_precharge_mosfets_1_out_2[6]),
    .out_10(adh_precharge_mosfets_1_out_2[7]));

  // Other names for the same wires on the sheet: _1171 = in_1
endmodule

module Clock_Generation (
  input  _1171,
  output _1163,
  output _421,
  output _710,
  output _943
);

  wire pull_resistor_2_node, pull_resistor_3_node, pull_resistor_6_node, transistor_3_out, transistor_6_out,
       transistor_8_out, transistor_12_out, transistor_14_out, transistor_17_out, transistor_19_out,
       transistor_20_out, transistor_28_out;

  Transistor #(.\type ("n")) transistor_1 (.in(1'b0), .out(_1171), .gate(1'b0));
  Transistor #(.\type ("n")) transistor_2 (.in(1'b0), .out(_1171), .gate(1'b0));
  Transistor #(.\type ("n")) transistor_3 (.in(1'b0), .out(transistor_3_out), .gate(_1171));
  Pull_Resistor #(.pull(1)) pull_resistor_1 (.node(transistor_3_out));
  Pull_Resistor #(.pull(1)) pull_resistor_2 (.node(pull_resistor_2_node));
  Transistor #(.\type ("n")) transistor_4 (.in(1'b0), .out(pull_resistor_2_node), .gate(_1171));
  Pull_Resistor #(.pull(1)) pull_resistor_3 (.node(pull_resistor_3_node));
  Transistor #(.\type ("n")) transistor_5 (.in(1'b0), .out(pull_resistor_3_node), .gate(transistor_3_out));
  Transistor #(.\type ("n")) transistor_6 (.in(1'b0), .out(transistor_6_out), .gate(transistor_3_out));
  Transistor #(.\type ("n")) transistor_7 (.in(1'b0), .out(transistor_6_out), .gate(transistor_3_out));
  Transistor #(.\type ("n")) transistor_8 (.in(1'b0), .out(transistor_8_out), .gate(pull_resistor_3_node));
  Pull_Resistor #(.pull(1)) pull_resistor_4 (.node(transistor_8_out));
  Transistor #(.\type ("n")) transistor_9 (.in(1'b0), .out(transistor_6_out), .gate(_710));
  Pull_Resistor #(.pull(1)) pull_resistor_5 (.node(transistor_6_out));
  Pull_Resistor #(.pull(1)) pull_resistor_6 (.node(pull_resistor_6_node));
  Transistor #(.\type ("n")) transistor_10 (.in(1'b0), .out(pull_resistor_6_node), .gate(pull_resistor_2_node));
  Transistor #(.\type ("n")) transistor_11 (.in(1'b0), .out(pull_resistor_6_node), .gate(pull_resistor_2_node));
  Transistor #(.\type ("n")) transistor_12 (.in(1'b0), .out(transistor_12_out), .gate(_710));
  Transistor #(.\type ("n")) transistor_13 (.in(1'b0), .out(transistor_12_out), .gate(pull_resistor_2_node));
  Pull_Resistor #(.pull(1)) pull_resistor_7 (.node(transistor_12_out));
  Transistor #(.\type ("n")) transistor_14 (.in(1'b1), .out(transistor_14_out), .gate(pull_resistor_3_node));
  Transistor #(.\type ("n")) transistor_15 (.in(1'b0), .out(transistor_14_out), .gate(transistor_8_out));
  Transistor #(.\type ("n")) transistor_16 (.in(1'b0), .out(transistor_8_out), .gate(pull_resistor_3_node));
  Transistor #(.\type ("n")) transistor_17 (.in(1'b1), .out(transistor_17_out), .gate(transistor_3_out));
  Transistor #(.\type ("n")) transistor_18 (.in(1'b0), .out(transistor_17_out), .gate(transistor_6_out));
  Transistor #(.\type ("n")) transistor_19 (.in(1'b0), .out(transistor_19_out), .gate(pull_resistor_6_node));
  Pull_Resistor #(.pull(1)) pull_resistor_8 (.node(transistor_19_out));
  Transistor #(.\type ("n")) transistor_20 (.in(1'b1), .out(transistor_20_out), .gate(pull_resistor_2_node));
  Transistor #(.\type ("n")) transistor_21 (.in(1'b0), .out(transistor_20_out), .gate(transistor_12_out));
  Transistor #(.\type ("n")) transistor_22 (.in(1'b1), .out(_710), .gate(transistor_8_out));
  Transistor #(.\type ("n")) transistor_23 (.in(1'b0), .out(_710), .gate(transistor_14_out));
  Transistor #(.\type ("n")) transistor_24 (.in(1'b0), .out(_710), .gate(transistor_14_out));
  Transistor #(.\type ("n")) transistor_25 (.in(1'b1), .out(_943), .gate(transistor_6_out));
  Transistor #(.\type ("n")) transistor_26 (.in(1'b0), .out(_943), .gate(transistor_17_out));
  Transistor #(.\type ("n")) transistor_27 (.in(1'b0), .out(_943), .gate(transistor_17_out));
  Transistor #(.\type ("n")) transistor_28 (.in(1'b1), .out(transistor_28_out), .gate(pull_resistor_6_node));
  Transistor #(.\type ("n")) transistor_29 (.in(1'b0), .out(transistor_28_out), .gate(transistor_19_out));
  Transistor #(.\type ("n")) transistor_30 (.in(1'b1), .out(_421), .gate(transistor_12_out));
  Transistor #(.\type ("n")) transistor_31 (.in(1'b0), .out(_421), .gate(transistor_20_out));
  Transistor #(.\type ("n")) transistor_32 (.in(1'b0), .out(_421), .gate(transistor_20_out));
  Transistor #(.\type ("n")) transistor_33 (.in(1'b0), .out(_710), .gate(transistor_14_out));
  Transistor #(.\type ("n")) transistor_34 (.in(1'b0), .out(_710), .gate(transistor_14_out));
  Transistor #(.\type ("n")) transistor_35 (.in(1'b0), .out(_943), .gate(transistor_17_out));
  Transistor #(.\type ("n")) transistor_36 (.in(1'b0), .out(_943), .gate(transistor_17_out));
  Transistor #(.\type ("n")) transistor_37 (.in(1'b1), .out(_1163), .gate(transistor_19_out));
  Transistor #(.\type ("n")) transistor_38 (.in(1'b0), .out(_1163), .gate(transistor_28_out));
  Transistor #(.\type ("n")) transistor_39 (.in(1'b0), .out(_421), .gate(transistor_20_out));
  Transistor #(.\type ("n")) transistor_40 (.in(1'b0), .out(_421), .gate(transistor_20_out));
  Transistor #(.\type ("n")) transistor_41 (.in(1'b0), .out(_710), .gate(transistor_14_out));
  Transistor #(.\type ("n")) transistor_42 (.in(1'b0), .out(_943), .gate(1'b0));
  Transistor #(.\type ("n")) transistor_43 (.in(1'b0), .out(_1163), .gate(transistor_28_out));
  Transistor #(.\type ("n")) transistor_44 (.in(1'b0), .out(_1163), .gate(transistor_28_out));
  Transistor #(.\type ("n")) transistor_45 (.in(1'b0), .out(_1163), .gate(transistor_28_out));
  Transistor #(.\type ("n")) transistor_46 (.in(1'b0), .out(_1163), .gate(transistor_28_out));

  // Notes on the sheet:
  //   t7
  //   t965
  //   t2120
  //   t1942
  //   358
  //   t2524
  //   t452 - t453
  //   519
  //   t311
  //   1715
  //   t1342 - t1343
  //   t2558
  //   670
  //   t2743 - t2744
  //   t1169
  //   t1168
  //   1399
  //   t1344
  //   t1709
  //   1129
  //   t1035
  //   t1999
  //   t492
  //   127
  //   t1919
  //   t2179
  //   t362
  //   1467
  //   747
  //   t1627
  //   t76
  //   135
  //   t1496 - t1500
  //   1105
  //   t3057 - t3060
  //   t481
  //   1417
  //   t3
  //   t2523
  //   t551 - t555
  //   t422 - t425
endmodule

module Databus_Tristate_Buffers (
  input  _353,
  input  _97,
  input  _746,
  input  _1634,
  input  _444,
  input  _1088,
  input  _1453,
  input  _1415,
  input  _63,
  output _1005,
  output _82,
  output _945,
  output _650,
  output _1393,
  output _175,
  output _1591,
  output _1349
);

  wire pull_resistor_4_node, transistor_1_out, transistor_3_out, transistor_5_out, transistor_9_out,
       transistor_11_out, transistor_13_out, transistor_15_out, transistor_17_out, transistor_20_out,
       transistor_23_out, transistor_26_out, transistor_29_out, transistor_32_out, transistor_35_out,
       transistor_38_out, transistor_41_out, transistor_44_out, transistor_47_out, transistor_50_out,
       transistor_53_out, transistor_56_out, transistor_59_out, transistor_62_out;

  Transistor #(.\type ("n")) transistor_1 (.in(1'b0), .out(transistor_1_out), .gate(_97));
  Transistor #(.\type ("n")) transistor_2 (.in(1'b0), .out(transistor_1_out), .gate(_353));
  Pull_Resistor #(.pull(1)) pull_resistor_1 (.node(transistor_1_out));
  Transistor #(.\type ("n")) transistor_3 (.in(1'b0), .out(transistor_3_out), .gate(_746));
  Transistor #(.\type ("n")) transistor_4 (.in(1'b0), .out(transistor_3_out), .gate(_353));
  Pull_Resistor #(.pull(1)) pull_resistor_2 (.node(transistor_3_out));
  Transistor #(.\type ("n")) transistor_5 (.in(1'b0), .out(transistor_5_out), .gate(_353));
  Transistor #(.\type ("n")) transistor_6 (.in(1'b0), .out(transistor_5_out), .gate(_1634));
  Pull_Resistor #(.pull(1)) pull_resistor_3 (.node(transistor_5_out));
  Pull_Resistor #(.pull(1)) pull_resistor_4 (.node(pull_resistor_4_node));
  Transistor #(.\type ("n")) transistor_7 (.in(1'b0), .out(pull_resistor_4_node), .gate(_353));
  Transistor #(.\type ("n")) transistor_8 (.in(1'b0), .out(pull_resistor_4_node), .gate(_444));
  Transistor #(.\type ("n")) transistor_9 (.in(1'b0), .out(transistor_9_out), .gate(_1088));
  Pull_Resistor #(.pull(1)) pull_resistor_5 (.node(transistor_9_out));
  Transistor #(.\type ("n")) transistor_10 (.in(1'b0), .out(transistor_9_out), .gate(_353));
  Transistor #(.\type ("n")) transistor_11 (.in(1'b0), .out(transistor_11_out), .gate(_1453));
  Transistor #(.\type ("n")) transistor_12 (.in(1'b0), .out(transistor_11_out), .gate(_353));
  Pull_Resistor #(.pull(1)) pull_resistor_6 (.node(transistor_11_out));
  Transistor #(.\type ("n")) transistor_13 (.in(1'b0), .out(transistor_13_out), .gate(_1415));
  Transistor #(.\type ("n")) transistor_14 (.in(1'b0), .out(transistor_13_out), .gate(_353));
  Pull_Resistor #(.pull(1)) pull_resistor_7 (.node(transistor_13_out));
  Transistor #(.\type ("n")) transistor_15 (.in(1'b0), .out(transistor_15_out), .gate(_353));
  Transistor #(.\type ("n")) transistor_16 (.in(1'b0), .out(transistor_15_out), .gate(_63));
  Pull_Resistor #(.pull(1)) pull_resistor_8 (.node(transistor_15_out));
  Transistor #(.\type ("n")) transistor_17 (.in(1'b1), .out(transistor_17_out), .gate(_97));
  Transistor #(.\type ("n")) transistor_18 (.in(1'b0), .out(transistor_17_out), .gate(_353));
  Transistor #(.\type ("n")) transistor_19 (.in(1'b0), .out(transistor_17_out), .gate(_353));
  Transistor #(.\type ("n")) transistor_20 (.in(1'b1), .out(transistor_20_out), .gate(transistor_1_out));
  Transistor #(.\type ("n")) transistor_21 (.in(1'b0), .out(transistor_20_out), .gate(_353));
  Transistor #(.\type ("n")) transistor_22 (.in(1'b0), .out(transistor_20_out), .gate(_353));
  Transistor #(.\type ("n")) transistor_23 (.in(1'b1), .out(transistor_23_out), .gate(_746));
  Transistor #(.\type ("n")) transistor_24 (.in(1'b0), .out(transistor_23_out), .gate(_353));
  Transistor #(.\type ("n")) transistor_25 (.in(1'b0), .out(transistor_23_out), .gate(_353));
  Transistor #(.\type ("n")) transistor_26 (.in(1'b1), .out(transistor_26_out), .gate(transistor_3_out));
  Transistor #(.\type ("n")) transistor_27 (.in(1'b0), .out(transistor_26_out), .gate(_353));
  Transistor #(.\type ("n")) transistor_28 (.in(1'b0), .out(transistor_26_out), .gate(_353));
  Transistor #(.\type ("n")) transistor_29 (.in(1'b1), .out(transistor_29_out), .gate(_1634));
  Transistor #(.\type ("n")) transistor_30 (.in(1'b0), .out(transistor_29_out), .gate(_353));
  Transistor #(.\type ("n")) transistor_31 (.in(1'b0), .out(transistor_29_out), .gate(_353));
  Transistor #(.\type ("n")) transistor_32 (.in(1'b1), .out(transistor_32_out), .gate(transistor_5_out));
  Transistor #(.\type ("n")) transistor_33 (.in(1'b0), .out(transistor_32_out), .gate(_353));
  Transistor #(.\type ("n")) transistor_34 (.in(1'b0), .out(transistor_32_out), .gate(_353));
  Transistor #(.\type ("n")) transistor_35 (.in(1'b1), .out(transistor_35_out), .gate(_444));
  Transistor #(.\type ("n")) transistor_36 (.in(1'b0), .out(transistor_35_out), .gate(_353));
  Transistor #(.\type ("n")) transistor_37 (.in(1'b0), .out(transistor_35_out), .gate(_353));
  Transistor #(.\type ("n")) transistor_38 (.in(1'b1), .out(transistor_38_out), .gate(pull_resistor_4_node));
  Transistor #(.\type ("n")) transistor_39 (.in(1'b0), .out(transistor_38_out), .gate(_353));
  Transistor #(.\type ("n")) transistor_40 (.in(1'b0), .out(transistor_38_out), .gate(_353));
  Transistor #(.\type ("n")) transistor_41 (.in(1'b1), .out(transistor_41_out), .gate(_1088));
  Transistor #(.\type ("n")) transistor_42 (.in(1'b0), .out(transistor_41_out), .gate(_353));
  Transistor #(.\type ("n")) transistor_43 (.in(1'b0), .out(transistor_41_out), .gate(_353));
  Transistor #(.\type ("n")) transistor_44 (.in(1'b1), .out(transistor_44_out), .gate(transistor_9_out));
  Transistor #(.\type ("n")) transistor_45 (.in(1'b0), .out(transistor_44_out), .gate(_353));
  Transistor #(.\type ("n")) transistor_46 (.in(1'b0), .out(transistor_44_out), .gate(_353));
  Transistor #(.\type ("n")) transistor_47 (.in(1'b1), .out(transistor_47_out), .gate(_1453));
  Transistor #(.\type ("n")) transistor_48 (.in(1'b0), .out(transistor_47_out), .gate(_353));
  Transistor #(.\type ("n")) transistor_49 (.in(1'b0), .out(transistor_47_out), .gate(_353));
  Transistor #(.\type ("n")) transistor_50 (.in(1'b1), .out(transistor_50_out), .gate(transistor_11_out));
  Transistor #(.\type ("n")) transistor_51 (.in(1'b0), .out(transistor_50_out), .gate(_353));
  Transistor #(.\type ("n")) transistor_52 (.in(1'b0), .out(transistor_50_out), .gate(_353));
  Transistor #(.\type ("n")) transistor_53 (.in(1'b1), .out(transistor_53_out), .gate(_1415));
  Transistor #(.\type ("n")) transistor_54 (.in(1'b0), .out(transistor_53_out), .gate(_353));
  Transistor #(.\type ("n")) transistor_55 (.in(1'b0), .out(transistor_53_out), .gate(_353));
  Transistor #(.\type ("n")) transistor_56 (.in(1'b1), .out(transistor_56_out), .gate(transistor_13_out));
  Transistor #(.\type ("n")) transistor_57 (.in(1'b0), .out(transistor_56_out), .gate(_353));
  Transistor #(.\type ("n")) transistor_58 (.in(1'b0), .out(transistor_56_out), .gate(_353));
  Transistor #(.\type ("n")) transistor_59 (.in(1'b1), .out(transistor_59_out), .gate(_63));
  Transistor #(.\type ("n")) transistor_60 (.in(1'b0), .out(transistor_59_out), .gate(_353));
  Transistor #(.\type ("n")) transistor_61 (.in(1'b0), .out(transistor_59_out), .gate(_353));
  Transistor #(.\type ("n")) transistor_62 (.in(1'b1), .out(transistor_62_out), .gate(transistor_15_out));
  Transistor #(.\type ("n")) transistor_63 (.in(1'b0), .out(transistor_62_out), .gate(_353));
  Transistor #(.\type ("n")) transistor_64 (.in(1'b0), .out(transistor_62_out), .gate(_353));
  Transistor #(.\type ("n")) transistor_65 (.in(1'b0), .out(transistor_17_out), .gate(transistor_1_out));
  Transistor #(.\type ("n")) transistor_66 (.in(1'b0), .out(transistor_20_out), .gate(_97));
  Transistor #(.\type ("n")) transistor_67 (.in(1'b0), .out(transistor_23_out), .gate(transistor_3_out));
  Transistor #(.\type ("n")) transistor_68 (.in(1'b0), .out(transistor_26_out), .gate(_746));
  Transistor #(.\type ("n")) transistor_69 (.in(1'b0), .out(transistor_29_out), .gate(transistor_5_out));
  Transistor #(.\type ("n")) transistor_70 (.in(1'b0), .out(transistor_32_out), .gate(_1634));
  Transistor #(.\type ("n")) transistor_71 (.in(1'b0), .out(transistor_35_out), .gate(pull_resistor_4_node));
  Transistor #(.\type ("n")) transistor_72 (.in(1'b0), .out(transistor_38_out), .gate(_444));
  Transistor #(.\type ("n")) transistor_73 (.in(1'b0), .out(transistor_41_out), .gate(transistor_9_out));
  Transistor #(.\type ("n")) transistor_74 (.in(1'b0), .out(transistor_44_out), .gate(_1088));
  Transistor #(.\type ("n")) transistor_75 (.in(1'b0), .out(transistor_47_out), .gate(transistor_11_out));
  Transistor #(.\type ("n")) transistor_76 (.in(1'b0), .out(transistor_50_out), .gate(_1453));
  Transistor #(.\type ("n")) transistor_77 (.in(1'b0), .out(transistor_53_out), .gate(transistor_13_out));
  Transistor #(.\type ("n")) transistor_78 (.in(1'b0), .out(transistor_56_out), .gate(_1415));
  Transistor #(.\type ("n")) transistor_79 (.in(1'b0), .out(transistor_59_out), .gate(transistor_15_out));
  Transistor #(.\type ("n")) transistor_80 (.in(1'b0), .out(transistor_62_out), .gate(_63));
  Transistor #(.\type ("n")) transistor_81 (.in(1'b1), .out(_1005), .gate(transistor_17_out));
  Transistor #(.\type ("n")) transistor_82 (.in(1'b1), .out(_1005), .gate(transistor_17_out));
  Transistor #(.\type ("n")) transistor_83 (.in(1'b0), .out(_1005), .gate(transistor_20_out));
  Transistor #(.\type ("n")) transistor_84 (.in(1'b0), .out(_1005), .gate(transistor_20_out));
  Transistor #(.\type ("n")) transistor_85 (.in(1'b1), .out(_82), .gate(transistor_23_out));
  Transistor #(.\type ("n")) transistor_86 (.in(1'b1), .out(_82), .gate(transistor_23_out));
  Transistor #(.\type ("n")) transistor_87 (.in(1'b0), .out(_82), .gate(transistor_26_out));
  Transistor #(.\type ("n")) transistor_88 (.in(1'b0), .out(_82), .gate(transistor_26_out));
  Transistor #(.\type ("n")) transistor_89 (.in(1'b1), .out(_945), .gate(transistor_29_out));
  Transistor #(.\type ("n")) transistor_90 (.in(1'b1), .out(_945), .gate(transistor_29_out));
  Transistor #(.\type ("n")) transistor_91 (.in(1'b0), .out(_945), .gate(transistor_32_out));
  Transistor #(.\type ("n")) transistor_92 (.in(1'b0), .out(_945), .gate(transistor_32_out));
  Transistor #(.\type ("n")) transistor_93 (.in(1'b1), .out(_650), .gate(transistor_35_out));
  Transistor #(.\type ("n")) transistor_94 (.in(1'b1), .out(_650), .gate(transistor_35_out));
  Transistor #(.\type ("n")) transistor_95 (.in(1'b0), .out(_650), .gate(transistor_38_out));
  Transistor #(.\type ("n")) transistor_96 (.in(1'b0), .out(_650), .gate(transistor_38_out));
  Transistor #(.\type ("n")) transistor_97 (.in(1'b1), .out(_1393), .gate(transistor_41_out));
  Transistor #(.\type ("n")) transistor_98 (.in(1'b1), .out(_1393), .gate(transistor_41_out));
  Transistor #(.\type ("n")) transistor_99 (.in(1'b0), .out(_1393), .gate(transistor_44_out));
  Transistor #(.\type ("n")) transistor_100 (.in(1'b0), .out(_1393), .gate(transistor_44_out));
  Transistor #(.\type ("n")) transistor_101 (.in(1'b1), .out(_175), .gate(transistor_47_out));
  Transistor #(.\type ("n")) transistor_102 (.in(1'b1), .out(_175), .gate(transistor_47_out));
  Transistor #(.\type ("n")) transistor_103 (.in(1'b0), .out(_175), .gate(transistor_50_out));
  Transistor #(.\type ("n")) transistor_104 (.in(1'b0), .out(_175), .gate(transistor_50_out));
  Transistor #(.\type ("n")) transistor_105 (.in(1'b1), .out(_1591), .gate(transistor_53_out));
  Transistor #(.\type ("n")) transistor_106 (.in(1'b1), .out(_1591), .gate(transistor_53_out));
  Transistor #(.\type ("n")) transistor_107 (.in(1'b0), .out(_1591), .gate(transistor_56_out));
  Transistor #(.\type ("n")) transistor_108 (.in(1'b0), .out(_1591), .gate(transistor_56_out));
  Transistor #(.\type ("n")) transistor_109 (.in(1'b1), .out(_1349), .gate(transistor_59_out));
  Transistor #(.\type ("n")) transistor_110 (.in(1'b1), .out(_1349), .gate(transistor_59_out));
  Transistor #(.\type ("n")) transistor_111 (.in(1'b0), .out(_1349), .gate(transistor_62_out));
  Transistor #(.\type ("n")) transistor_112 (.in(1'b0), .out(_1349), .gate(transistor_62_out));
  Transistor #(.\type ("n")) transistor_113 (.in(1'b0), .out(_1005), .gate(transistor_20_out));
  Transistor #(.\type ("n")) transistor_114 (.in(1'b0), .out(_1005), .gate(transistor_20_out));
  Transistor #(.\type ("n")) transistor_115 (.in(1'b0), .out(_82), .gate(transistor_26_out));
  Transistor #(.\type ("n")) transistor_116 (.in(1'b0), .out(_82), .gate(transistor_26_out));
  Transistor #(.\type ("n")) transistor_117 (.in(1'b0), .out(_945), .gate(transistor_32_out));
  Transistor #(.\type ("n")) transistor_118 (.in(1'b0), .out(_945), .gate(transistor_32_out));
  Transistor #(.\type ("n")) transistor_119 (.in(1'b0), .out(_650), .gate(transistor_38_out));
  Transistor #(.\type ("n")) transistor_120 (.in(1'b0), .out(_650), .gate(transistor_38_out));
  Transistor #(.\type ("n")) transistor_121 (.in(1'b0), .out(_1393), .gate(transistor_44_out));
  Transistor #(.\type ("n")) transistor_122 (.in(1'b0), .out(_1393), .gate(transistor_44_out));
  Transistor #(.\type ("n")) transistor_123 (.in(1'b0), .out(_175), .gate(transistor_50_out));
  Transistor #(.\type ("n")) transistor_124 (.in(1'b0), .out(_175), .gate(transistor_50_out));
  Transistor #(.\type ("n")) transistor_125 (.in(1'b0), .out(_1591), .gate(transistor_56_out));
  Transistor #(.\type ("n")) transistor_126 (.in(1'b0), .out(_1591), .gate(transistor_56_out));
  Transistor #(.\type ("n")) transistor_127 (.in(1'b0), .out(_1349), .gate(transistor_62_out));
  Transistor #(.\type ("n")) transistor_128 (.in(1'b0), .out(_1349), .gate(transistor_62_out));
  Transistor #(.\type ("n")) transistor_129 (.in(1'b0), .out(_1005), .gate(transistor_20_out));
  Transistor #(.\type ("n")) transistor_130 (.in(1'b0), .out(_1005), .gate(transistor_20_out));
  Transistor #(.\type ("n")) transistor_131 (.in(1'b0), .out(_82), .gate(transistor_26_out));
  Transistor #(.\type ("n")) transistor_132 (.in(1'b0), .out(_82), .gate(transistor_26_out));
  Transistor #(.\type ("n")) transistor_133 (.in(1'b0), .out(_945), .gate(transistor_32_out));
  Transistor #(.\type ("n")) transistor_134 (.in(1'b0), .out(_945), .gate(transistor_32_out));
  Transistor #(.\type ("n")) transistor_135 (.in(1'b0), .out(_650), .gate(transistor_38_out));
  Transistor #(.\type ("n")) transistor_136 (.in(1'b0), .out(_650), .gate(transistor_38_out));
  Transistor #(.\type ("n")) transistor_137 (.in(1'b0), .out(_1393), .gate(transistor_44_out));
  Transistor #(.\type ("n")) transistor_138 (.in(1'b0), .out(_1393), .gate(transistor_44_out));
  Transistor #(.\type ("n")) transistor_139 (.in(1'b0), .out(_175), .gate(transistor_50_out));
  Transistor #(.\type ("n")) transistor_140 (.in(1'b0), .out(_175), .gate(transistor_50_out));
  Transistor #(.\type ("n")) transistor_141 (.in(1'b0), .out(_1591), .gate(transistor_56_out));
  Transistor #(.\type ("n")) transistor_142 (.in(1'b0), .out(_1591), .gate(transistor_56_out));
  Transistor #(.\type ("n")) transistor_143 (.in(1'b0), .out(_1349), .gate(transistor_62_out));
  Transistor #(.\type ("n")) transistor_144 (.in(1'b0), .out(_1349), .gate(transistor_62_out));
  Transistor #(.\type ("n")) transistor_145 (.in(1'b0), .out(_1005), .gate(transistor_20_out));
  Transistor #(.\type ("n")) transistor_146 (.in(1'b0), .out(_1005), .gate(transistor_20_out));
  Transistor #(.\type ("n")) transistor_147 (.in(1'b0), .out(_82), .gate(transistor_26_out));
  Transistor #(.\type ("n")) transistor_148 (.in(1'b0), .out(_945), .gate(transistor_32_out));
  Transistor #(.\type ("n")) transistor_149 (.in(1'b0), .out(_945), .gate(transistor_32_out));
  Transistor #(.\type ("n")) transistor_150 (.in(1'b0), .out(_650), .gate(transistor_38_out));
  Transistor #(.\type ("n")) transistor_151 (.in(1'b0), .out(_1393), .gate(transistor_44_out));
  Transistor #(.\type ("n")) transistor_152 (.in(1'b0), .out(_1393), .gate(transistor_44_out));
  Transistor #(.\type ("n")) transistor_153 (.in(1'b0), .out(_175), .gate(transistor_50_out));
  Transistor #(.\type ("n")) transistor_154 (.in(1'b0), .out(_1591), .gate(transistor_56_out));
  Transistor #(.\type ("n")) transistor_155 (.in(1'b0), .out(_1349), .gate(transistor_62_out));
  Transistor #(.\type ("n")) transistor_156 (.in(1'b0), .out(_1005), .gate(1'b0));
  Transistor #(.\type ("n")) transistor_157 (.in(1'b0), .out(_82), .gate(1'b0));
  Transistor #(.\type ("n")) transistor_158 (.in(1'b0), .out(_945), .gate(transistor_32_out));
  Transistor #(.\type ("n")) transistor_159 (.in(1'b0), .out(_945), .gate(1'b0));
  Transistor #(.\type ("n")) transistor_160 (.in(1'b0), .out(_650), .gate(1'b0));
  Transistor #(.\type ("n")) transistor_161 (.in(1'b0), .out(_1393), .gate(transistor_44_out));
  Transistor #(.\type ("n")) transistor_162 (.in(1'b0), .out(_1393), .gate(1'b0));
  Transistor #(.\type ("n")) transistor_163 (.in(1'b0), .out(_175), .gate(1'b0));
  Transistor #(.\type ("n")) transistor_164 (.in(1'b0), .out(_1591), .gate(1'b0));
  Transistor #(.\type ("n")) transistor_165 (.in(1'b0), .out(_1349), .gate(1'b0));

  // Notes on the sheet:
  //   t1034
  //   t1971
  //   t560
  //   t1492
  //   t2206
  //   t1632
  //   t1418
  //   t1569
  //   t2651
  //   t1032 - t1033
  //   769
  //   t3035
  //   t2574 - t2575
  //   t333
  //   t1630 - t1631
  //   288
  //   t1515
  //   t50 - t51
  //   t578
  //   t1416 - t1417
  //   224
  //   t3122
  //   t1510 - t1511
  //   t1254
  //   t1567 - t1568
  //   1613
  //   t2516
  //   t1609 - t1610
  //   t3034
  //   1072
  //   t2205
  //   t1514
  //   794
  //   t1970
  //   t3121
  //   37
  //   t559
  //   t2515
  //   42
  //   643
  //   t1491
  //   147
  //   1325
  //   t1712 - t1713
  //   798
  //   t154 - t155
  //   520
  //   t1536- t1537
  //   t1679 - t1680
  //   1076
  //   t382 - t383
  //   t3473 - t3480
  //   t3410 - t3416
  //   t1887 - t1893
  //   t3037 - t3045
  //   t1088 - t1096
  //   t2083
  //   t364
  //   t1445
  //   t65
  //   t3227
  //   In visual6502 1088 is listed twice, and shown as connected back to 945.  Shown here tied back to ground for digital logic to work.
endmodule

module Data_Output_Register (
  input  _710,
  input  _1108,
  input  _991,
  input  _1473,
  input  _1302,
  input  _892,
  input  _1503,
  input  _833,
  input  _493,
  output _97,
  output _746,
  output _1634,
  output _444,
  output _1088,
  output _1453,
  output _1415,
  output _63
);

  wire pull_resistor_2_node, register_1_q, register_2_q, register_3_q, register_4_q, register_5_q,
       register_6_q, register_7_q, register_8_q, transistor_1_out, transistor_3_out, transistor_4_out,
       transistor_5_out, transistor_6_out, transistor_7_out, transistor_8_out, transistor_9_out,
       transistor_10_out, transistor_11_out, transistor_12_out, transistor_13_out, transistor_14_out,
       transistor_15_out, transistor_16_out;

  Transistor #(.\type ("n")) transistor_1 (.in(1'b0), .out(transistor_1_out), .gate(_1108));
  Pull_Resistor #(.pull(1)) pull_resistor_1 (.node(transistor_1_out));
  Pull_Resistor #(.pull(1)) pull_resistor_2 (.node(pull_resistor_2_node));
  Transistor #(.\type ("n")) transistor_2 (.in(1'b0), .out(pull_resistor_2_node), .gate(_991));
  Transistor #(.\type ("n")) transistor_3 (.in(1'b0), .out(transistor_3_out), .gate(_1473));
  Pull_Resistor #(.pull(1)) pull_resistor_3 (.node(transistor_3_out));
  Transistor #(.\type ("n")) transistor_4 (.in(1'b0), .out(transistor_4_out), .gate(_1302));
  Pull_Resistor #(.pull(1)) pull_resistor_4 (.node(transistor_4_out));
  Transistor #(.\type ("n")) transistor_5 (.in(1'b0), .out(transistor_5_out), .gate(_892));
  Pull_Resistor #(.pull(1)) pull_resistor_5 (.node(transistor_5_out));
  Transistor #(.\type ("n")) transistor_6 (.in(1'b0), .out(transistor_6_out), .gate(_1503));
  Pull_Resistor #(.pull(1)) pull_resistor_6 (.node(transistor_6_out));
  Transistor #(.\type ("n")) transistor_7 (.in(1'b0), .out(transistor_7_out), .gate(_833));
  Pull_Resistor #(.pull(1)) pull_resistor_7 (.node(transistor_7_out));
  Transistor #(.\type ("n")) transistor_8 (.in(1'b0), .out(transistor_8_out), .gate(_493));
  Pull_Resistor #(.pull(1)) pull_resistor_8 (.node(transistor_8_out));
  Transistor #(.\type ("n")) transistor_9 (.in(transistor_1_out), .out(transistor_9_out), .gate(_710));
  Transistor #(.\type ("n")) transistor_10 (.in(pull_resistor_2_node), .out(transistor_10_out), .gate(_710));
  Transistor #(.\type ("n")) transistor_11 (.in(transistor_3_out), .out(transistor_11_out), .gate(_710));
  Transistor #(.\type ("n")) transistor_12 (.in(transistor_4_out), .out(transistor_12_out), .gate(_710));
  Transistor #(.\type ("n")) transistor_13 (.in(transistor_5_out), .out(transistor_13_out), .gate(_710));
  Transistor #(.\type ("n")) transistor_14 (.in(transistor_6_out), .out(transistor_14_out), .gate(_710));
  Transistor #(.\type ("n")) transistor_15 (.in(transistor_7_out), .out(transistor_15_out), .gate(_710));
  Transistor #(.\type ("n")) transistor_16 (.in(transistor_8_out), .out(transistor_16_out), .gate(_710));
  Transistor #(.\type ("n")) transistor_17 (.in(1'b0), .out(_97), .gate(register_1_q));
  Register #(.width(1), .trigger("high")) register_1 (
    .D(transistor_9_out), .Q(register_1_q), .clk(_710));  // open: en, clr
  Transistor #(.\type ("n")) transistor_18 (.in(1'b0), .out(_746), .gate(register_2_q));
  Register #(.width(1), .trigger("high")) register_2 (
    .D(transistor_10_out), .Q(register_2_q), .clk(_710));  // open: en, clr
  Transistor #(.\type ("n")) transistor_19 (.in(1'b0), .out(_1634), .gate(register_3_q));
  Register #(.width(1), .trigger("high")) register_3 (
    .D(transistor_11_out), .Q(register_3_q), .clk(_710));  // open: en, clr
  Transistor #(.\type ("n")) transistor_20 (.in(1'b0), .out(_444), .gate(register_4_q));
  Register #(.width(1), .trigger("high")) register_4 (
    .D(transistor_12_out), .Q(register_4_q), .clk(_710));  // open: en, clr
  Transistor #(.\type ("n")) transistor_21 (.in(1'b0), .out(_1088), .gate(register_5_q));
  Register #(.width(1), .trigger("high")) register_5 (
    .D(transistor_13_out), .Q(register_5_q), .clk(_710));  // open: en, clr
  Transistor #(.\type ("n")) transistor_22 (.in(1'b0), .out(_1453), .gate(register_6_q));
  Register #(.width(1), .trigger("high")) register_6 (
    .D(transistor_14_out), .Q(register_6_q), .clk(_710));  // open: en, clr
  Transistor #(.\type ("n")) transistor_23 (.in(1'b0), .out(_1415), .gate(register_7_q));
  Register #(.width(1), .trigger("high")) register_7 (
    .D(transistor_15_out), .Q(register_7_q), .clk(_710));  // open: en, clr
  Transistor #(.\type ("n")) transistor_24 (.in(1'b0), .out(_63), .gate(register_8_q));
  Register #(.width(1), .trigger("high")) register_8 (
    .D(transistor_16_out), .Q(register_8_q), .clk(_710));  // open: en, clr
  Pull_Resistor #(.pull(1)) pull_resistor_9 (.node(_97));
  Pull_Resistor #(.pull(1)) pull_resistor_10 (.node(_746));
  Pull_Resistor #(.pull(1)) pull_resistor_11 (.node(_1634));
  Pull_Resistor #(.pull(1)) pull_resistor_12 (.node(_444));
  Pull_Resistor #(.pull(1)) pull_resistor_13 (.node(_1088));
  Pull_Resistor #(.pull(1)) pull_resistor_14 (.node(_1453));
  Pull_Resistor #(.pull(1)) pull_resistor_15 (.node(_1415));
  Pull_Resistor #(.pull(1)) pull_resistor_16 (.node(_63));

  // Notes on the sheet:
  //   1687
  //   t2892
  //   t1264
  //   222
  //   t2140
endmodule

module Predecode_Register (
  input  _943,
  input  in_2,
  input  in_3,
  input  in_4,
  input  in_5,
  input  in_6,
  input  in_7,
  input  in_8,
  input  in_9,
  output _758,
  output _361,
  output _955,
  output _894,
  output _369,
  output _829,
  output _1669,
  output _1690
);

  wire pull_resistor_1_node, pull_resistor_2_node, pull_resistor_3_node, register_1_q, register_2_q,
       register_3_q, register_4_q, register_5_q, register_6_q, register_7_q, register_8_q, transistor_4_out,
       transistor_5_out, transistor_6_out, transistor_7_out, transistor_8_out, transistor_9_out,
       transistor_10_out, transistor_11_out, transistor_12_out, transistor_13_out, transistor_14_out,
       transistor_15_out, transistor_16_out;

  Pull_Resistor #(.pull(1)) pull_resistor_1 (.node(pull_resistor_1_node));
  Transistor #(.\type ("n")) transistor_1 (.in(1'b0), .out(pull_resistor_1_node), .gate(in_2));
  Pull_Resistor #(.pull(1)) pull_resistor_2 (.node(pull_resistor_2_node));
  Transistor #(.\type ("n")) transistor_2 (.in(1'b0), .out(pull_resistor_2_node), .gate(in_3));
  Pull_Resistor #(.pull(1)) pull_resistor_3 (.node(pull_resistor_3_node));
  Transistor #(.\type ("n")) transistor_3 (.in(1'b0), .out(pull_resistor_3_node), .gate(in_4));
  Transistor #(.\type ("n")) transistor_4 (.in(1'b0), .out(transistor_4_out), .gate(in_5));
  Pull_Resistor #(.pull(1)) pull_resistor_4 (.node(transistor_4_out));
  Transistor #(.\type ("n")) transistor_5 (.in(1'b0), .out(transistor_5_out), .gate(in_6));
  Pull_Resistor #(.pull(1)) pull_resistor_5 (.node(transistor_5_out));
  Transistor #(.\type ("n")) transistor_6 (.in(1'b0), .out(transistor_6_out), .gate(in_7));
  Pull_Resistor #(.pull(1)) pull_resistor_6 (.node(transistor_6_out));
  Transistor #(.\type ("n")) transistor_7 (.in(1'b0), .out(transistor_7_out), .gate(in_8));
  Pull_Resistor #(.pull(1)) pull_resistor_7 (.node(transistor_7_out));
  Transistor #(.\type ("n")) transistor_8 (.in(1'b0), .out(transistor_8_out), .gate(in_9));
  Pull_Resistor #(.pull(1)) pull_resistor_8 (.node(transistor_8_out));
  Transistor #(.\type ("n")) transistor_9 (.in(pull_resistor_1_node), .out(transistor_9_out), .gate(_943));
  Transistor #(.\type ("n")) transistor_10 (.in(pull_resistor_2_node), .out(transistor_10_out), .gate(_943));
  Transistor #(.\type ("n")) transistor_11 (.in(pull_resistor_3_node), .out(transistor_11_out), .gate(_943));
  Transistor #(.\type ("n")) transistor_12 (.in(transistor_4_out), .out(transistor_12_out), .gate(_943));
  Transistor #(.\type ("n")) transistor_13 (.in(transistor_5_out), .out(transistor_13_out), .gate(_943));
  Transistor #(.\type ("n")) transistor_14 (.in(transistor_6_out), .out(transistor_14_out), .gate(_943));
  Transistor #(.\type ("n")) transistor_15 (.in(transistor_7_out), .out(transistor_15_out), .gate(_943));
  Transistor #(.\type ("n")) transistor_16 (.in(transistor_8_out), .out(transistor_16_out), .gate(_943));
  Transistor #(.\type ("n")) transistor_17 (.in(1'b0), .out(_758), .gate(register_1_q));
  Register #(.width(1), .trigger("high")) register_1 (
    .D(transistor_9_out), .Q(register_1_q), .clk(_943));  // open: en, clr
  Transistor #(.\type ("n")) transistor_18 (.in(1'b0), .out(_361), .gate(register_2_q));
  Register #(.width(1), .trigger("high")) register_2 (
    .D(transistor_10_out), .Q(register_2_q), .clk(_943));  // open: en, clr
  Transistor #(.\type ("n")) transistor_19 (.in(1'b0), .out(_955), .gate(register_3_q));
  Register #(.width(1), .trigger("high")) register_3 (
    .D(transistor_11_out), .Q(register_3_q), .clk(_943));  // open: en, clr
  Transistor #(.\type ("n")) transistor_20 (.in(1'b0), .out(_894), .gate(register_4_q));
  Register #(.width(1), .trigger("high")) register_4 (
    .D(transistor_12_out), .Q(register_4_q), .clk(_943));  // open: en, clr
  Transistor #(.\type ("n")) transistor_21 (.in(1'b0), .out(_369), .gate(register_5_q));
  Register #(.width(1), .trigger("high")) register_5 (
    .D(transistor_13_out), .Q(register_5_q), .clk(_943));  // open: en, clr
  Transistor #(.\type ("n")) transistor_22 (.in(1'b0), .out(_829), .gate(register_6_q));
  Register #(.width(1), .trigger("high")) register_6 (
    .D(transistor_14_out), .Q(register_6_q), .clk(_943));  // open: en, clr
  Transistor #(.\type ("n")) transistor_23 (.in(1'b0), .out(_1669), .gate(register_7_q));
  Register #(.width(1), .trigger("high")) register_7 (
    .D(transistor_15_out), .Q(register_7_q), .clk(_943));  // open: en, clr
  Transistor #(.\type ("n")) transistor_24 (.in(1'b0), .out(_1690), .gate(register_8_q));
  Register #(.width(1), .trigger("high")) register_8 (
    .D(transistor_16_out), .Q(register_8_q), .clk(_943));  // open: en, clr
  Pull_Resistor #(.pull(1)) pull_resistor_9 (.node(_758));
  Pull_Resistor #(.pull(1)) pull_resistor_10 (.node(_361));
  Pull_Resistor #(.pull(1)) pull_resistor_11 (.node(_955));
  Pull_Resistor #(.pull(1)) pull_resistor_12 (.node(_894));
  Pull_Resistor #(.pull(1)) pull_resistor_13 (.node(_369));
  Pull_Resistor #(.pull(1)) pull_resistor_14 (.node(_829));
  Pull_Resistor #(.pull(1)) pull_resistor_15 (.node(_1669));
  Pull_Resistor #(.pull(1)) pull_resistor_16 (.node(_1690));
endmodule

module Input_Data_Latch (
  input  _943,
  input  in_2,
  input  in_3,
  input  in_4,
  input  in_5,
  input  in_6,
  input  in_7,
  input  in_8,
  input  in_9,
  input  in_10,
  input  in_11,
  input  in_12
);

  wire pull_resistor_5_node, pull_resistor_6_node, pull_resistor_7_node, pull_resistor_8_node, register_1_q,
       register_2_q, register_3_q, register_4_q, register_5_q, register_6_q, register_7_q, register_8_q,
       transistor_1_out, transistor_2_out, transistor_3_out, transistor_4_out, transistor_9_out,
       transistor_10_out, transistor_11_out, transistor_12_out, transistor_13_out, transistor_14_out,
       transistor_15_out, transistor_16_out, transistor_17_out, transistor_18_out, transistor_19_out,
       transistor_20_out, transistor_21_out, transistor_22_out, transistor_23_out, transistor_24_out,
       transistor_25_out, transistor_26_out, transistor_27_out, transistor_28_out, transistor_29_out,
       transistor_30_out, transistor_31_out, transistor_32_out, transistor_33_out, transistor_34_out,
       transistor_35_out, transistor_36_out, transistor_37_out, transistor_38_out, transistor_39_out,
       transistor_40_out, transistor_41_out, transistor_42_out, transistor_43_out, transistor_44_out,
       transistor_45_out, transistor_46_out, transistor_47_out, transistor_48_out;

  Transistor #(.\type ("n")) transistor_1 (.in(1'b0), .out(transistor_1_out), .gate(in_2));
  Pull_Resistor #(.pull(1)) pull_resistor_1 (.node(transistor_1_out));
  Transistor #(.\type ("n")) transistor_2 (.in(1'b0), .out(transistor_2_out), .gate(in_3));
  Pull_Resistor #(.pull(1)) pull_resistor_2 (.node(transistor_2_out));
  Transistor #(.\type ("n")) transistor_3 (.in(1'b0), .out(transistor_3_out), .gate(in_4));
  Pull_Resistor #(.pull(1)) pull_resistor_3 (.node(transistor_3_out));
  Transistor #(.\type ("n")) transistor_4 (.in(1'b0), .out(transistor_4_out), .gate(in_5));
  Pull_Resistor #(.pull(1)) pull_resistor_4 (.node(transistor_4_out));
  Pull_Resistor #(.pull(1)) pull_resistor_5 (.node(pull_resistor_5_node));
  Transistor #(.\type ("n")) transistor_5 (.in(1'b0), .out(pull_resistor_5_node), .gate(in_6));
  Pull_Resistor #(.pull(1)) pull_resistor_6 (.node(pull_resistor_6_node));
  Transistor #(.\type ("n")) transistor_6 (.in(1'b0), .out(pull_resistor_6_node), .gate(in_7));
  Pull_Resistor #(.pull(1)) pull_resistor_7 (.node(pull_resistor_7_node));
  Transistor #(.\type ("n")) transistor_7 (.in(1'b0), .out(pull_resistor_7_node), .gate(in_8));
  Pull_Resistor #(.pull(1)) pull_resistor_8 (.node(pull_resistor_8_node));
  Transistor #(.\type ("n")) transistor_8 (.in(1'b0), .out(pull_resistor_8_node), .gate(in_9));
  Transistor #(.\type ("n")) transistor_9 (.in(transistor_1_out), .out(transistor_9_out), .gate(_943));
  Transistor #(.\type ("n")) transistor_10 (.in(transistor_2_out), .out(transistor_10_out), .gate(_943));
  Transistor #(.\type ("n")) transistor_11 (.in(transistor_3_out), .out(transistor_11_out), .gate(_943));
  Transistor #(.\type ("n")) transistor_12 (.in(transistor_4_out), .out(transistor_12_out), .gate(_943));
  Transistor #(.\type ("n")) transistor_13 (.in(pull_resistor_5_node), .out(transistor_13_out), .gate(_943));
  Transistor #(.\type ("n")) transistor_14 (.in(pull_resistor_6_node), .out(transistor_14_out), .gate(_943));
  Transistor #(.\type ("n")) transistor_15 (.in(pull_resistor_7_node), .out(transistor_15_out), .gate(_943));
  Transistor #(.\type ("n")) transistor_16 (.in(pull_resistor_8_node), .out(transistor_16_out), .gate(_943));
  Transistor #(.\type ("n")) transistor_17 (.in(1'b0), .out(transistor_17_out), .gate(register_1_q));
  Register #(.width(1), .trigger("high")) register_1 (
    .D(transistor_9_out), .Q(register_1_q), .clk(_943));  // open: en, clr
  Transistor #(.\type ("n")) transistor_18 (.in(1'b0), .out(transistor_18_out), .gate(register_2_q));
  Register #(.width(1), .trigger("high")) register_2 (
    .D(transistor_10_out), .Q(register_2_q), .clk(_943));  // open: en, clr
  Transistor #(.\type ("n")) transistor_19 (.in(1'b0), .out(transistor_19_out), .gate(register_3_q));
  Register #(.width(1), .trigger("high")) register_3 (
    .D(transistor_11_out), .Q(register_3_q), .clk(_943));  // open: en, clr
  Transistor #(.\type ("n")) transistor_20 (.in(1'b0), .out(transistor_20_out), .gate(register_4_q));
  Register #(.width(1), .trigger("high")) register_4 (
    .D(transistor_12_out), .Q(register_4_q), .clk(_943));  // open: en, clr
  Transistor #(.\type ("n")) transistor_21 (.in(1'b0), .out(transistor_21_out), .gate(register_5_q));
  Register #(.width(1), .trigger("high")) register_5 (
    .D(transistor_13_out), .Q(register_5_q), .clk(_943));  // open: en, clr
  Transistor #(.\type ("n")) transistor_22 (.in(1'b0), .out(transistor_22_out), .gate(register_6_q));
  Register #(.width(1), .trigger("high")) register_6 (
    .D(transistor_14_out), .Q(register_6_q), .clk(_943));  // open: en, clr
  Transistor #(.\type ("n")) transistor_23 (.in(1'b0), .out(transistor_23_out), .gate(register_7_q));
  Register #(.width(1), .trigger("high")) register_7 (
    .D(transistor_15_out), .Q(register_7_q), .clk(_943));  // open: en, clr
  Transistor #(.\type ("n")) transistor_24 (.in(1'b0), .out(transistor_24_out), .gate(register_8_q));
  Register #(.width(1), .trigger("high")) register_8 (
    .D(transistor_16_out), .Q(register_8_q), .clk(_943));  // open: en, clr
  Pull_Resistor #(.pull(1)) pull_resistor_9 (.node(transistor_17_out));
  Transistor #(.\type ("n")) transistor_25 (.in(transistor_17_out), .out(transistor_25_out), .gate(in_10));
  Pull_Resistor #(.pull(1)) pull_resistor_10 (.node(transistor_18_out));
  Transistor #(.\type ("n")) transistor_26 (.in(transistor_18_out), .out(transistor_26_out), .gate(in_10));
  Pull_Resistor #(.pull(1)) pull_resistor_11 (.node(transistor_19_out));
  Transistor #(.\type ("n")) transistor_27 (.in(transistor_19_out), .out(transistor_27_out), .gate(in_10));
  Pull_Resistor #(.pull(1)) pull_resistor_12 (.node(transistor_20_out));
  Transistor #(.\type ("n")) transistor_28 (.in(transistor_20_out), .out(transistor_28_out), .gate(in_10));
  Pull_Resistor #(.pull(1)) pull_resistor_13 (.node(transistor_21_out));
  Transistor #(.\type ("n")) transistor_29 (.in(transistor_21_out), .out(transistor_29_out), .gate(in_10));
  Pull_Resistor #(.pull(1)) pull_resistor_14 (.node(transistor_22_out));
  Transistor #(.\type ("n")) transistor_30 (.in(transistor_22_out), .out(transistor_30_out), .gate(in_10));
  Pull_Resistor #(.pull(1)) pull_resistor_15 (.node(transistor_23_out));
  Transistor #(.\type ("n")) transistor_31 (.in(transistor_23_out), .out(transistor_31_out), .gate(in_10));
  Pull_Resistor #(.pull(1)) pull_resistor_16 (.node(transistor_24_out));
  Transistor #(.\type ("n")) transistor_32 (.in(transistor_24_out), .out(transistor_32_out), .gate(in_10));
  Transistor #(.\type ("n")) transistor_33 (.in(transistor_17_out), .out(transistor_33_out), .gate(in_11));
  Transistor #(.\type ("n")) transistor_34 (.in(transistor_18_out), .out(transistor_34_out), .gate(in_11));
  Transistor #(.\type ("n")) transistor_35 (.in(transistor_19_out), .out(transistor_35_out), .gate(in_11));
  Transistor #(.\type ("n")) transistor_36 (.in(transistor_20_out), .out(transistor_36_out), .gate(in_11));
  Transistor #(.\type ("n")) transistor_37 (.in(transistor_21_out), .out(transistor_37_out), .gate(in_11));
  Transistor #(.\type ("n")) transistor_38 (.in(transistor_22_out), .out(transistor_38_out), .gate(in_11));
  Transistor #(.\type ("n")) transistor_39 (.in(transistor_23_out), .out(transistor_39_out), .gate(in_11));
  Transistor #(.\type ("n")) transistor_40 (.in(transistor_24_out), .out(transistor_40_out), .gate(in_11));
  Transistor #(.\type ("n")) transistor_41 (.in(transistor_17_out), .out(transistor_41_out), .gate(in_12));
  Transistor #(.\type ("n")) transistor_42 (.in(transistor_18_out), .out(transistor_42_out), .gate(in_12));
  Transistor #(.\type ("n")) transistor_43 (.in(transistor_19_out), .out(transistor_43_out), .gate(in_12));
  Transistor #(.\type ("n")) transistor_44 (.in(transistor_20_out), .out(transistor_44_out), .gate(in_12));
  Transistor #(.\type ("n")) transistor_45 (.in(transistor_21_out), .out(transistor_45_out), .gate(in_12));
  Transistor #(.\type ("n")) transistor_46 (.in(transistor_22_out), .out(transistor_46_out), .gate(in_12));
  Transistor #(.\type ("n")) transistor_47 (.in(transistor_23_out), .out(transistor_47_out), .gate(in_12));
  Transistor #(.\type ("n")) transistor_48 (.in(transistor_24_out), .out(transistor_48_out), .gate(in_12));
endmodule

module Databus_Precharge_Mosfets (
  input  _943,
  output out_2,
  output out_3,
  output out_4,
  output out_5,
  output out_6,
  output out_7,
  output out_8,
  output out_9
);

  Transistor #(.\type ("n")) transistor_1 (.in(1'b1), .out(out_2), .gate(_943));
  Transistor #(.\type ("n")) transistor_2 (.in(1'b1), .out(out_3), .gate(_943));
  Transistor #(.\type ("n")) transistor_3 (.in(1'b1), .out(out_4), .gate(_943));
  Transistor #(.\type ("n")) transistor_4 (.in(1'b1), .out(out_5), .gate(_943));
  Transistor #(.\type ("n")) transistor_5 (.in(1'b1), .out(out_6), .gate(_943));
  Transistor #(.\type ("n")) transistor_6 (.in(1'b1), .out(out_7), .gate(_943));
  Transistor #(.\type ("n")) transistor_7 (.in(1'b1), .out(out_8), .gate(_943));
  Transistor #(.\type ("n")) transistor_8 (.in(1'b1), .out(out_9), .gate(_943));
endmodule

module Predecode_Logic (
  input  _1077,
  input  _710,
  input  _724,
  input  in_4,
  input  in_5,
  input  in_6,
  input  in_7,
  input  in_8,
  input  in_9,
  input  in_10,
  input  in_11,
  output out_12,
  output out_13,
  output out_14,
  output out_15,
  output out_16,
  output out_17,
  output out_18,
  output out_19
);

  wire pull_resistor_1_node, pull_resistor_2_node, pull_resistor_3_node, pull_resistor_4_node,
       pull_resistor_5_node, pull_resistor_6_node, pull_resistor_7_node, pull_resistor_8_node,
       transistor_17_out, transistor_18_out, transistor_19_out, transistor_20_out, transistor_21_out,
       transistor_22_out, transistor_23_out, transistor_24_out;

  Pull_Resistor #(.pull(1)) pull_resistor_1 (.node(pull_resistor_1_node));
  Transistor #(.\type ("n")) transistor_1 (.in(1'b0), .out(pull_resistor_1_node), .gate(in_4));
  Transistor #(.\type ("n")) transistor_2 (.in(1'b0), .out(pull_resistor_1_node), .gate(_1077));
  Pull_Resistor #(.pull(1)) pull_resistor_2 (.node(pull_resistor_2_node));
  Transistor #(.\type ("n")) transistor_3 (.in(1'b0), .out(pull_resistor_2_node), .gate(_1077));
  Transistor #(.\type ("n")) transistor_4 (.in(1'b0), .out(pull_resistor_2_node), .gate(in_5));
  Pull_Resistor #(.pull(1)) pull_resistor_3 (.node(pull_resistor_3_node));
  Transistor #(.\type ("n")) transistor_5 (.in(1'b0), .out(pull_resistor_3_node), .gate(_1077));
  Transistor #(.\type ("n")) transistor_6 (.in(1'b0), .out(pull_resistor_3_node), .gate(in_6));
  Pull_Resistor #(.pull(1)) pull_resistor_4 (.node(pull_resistor_4_node));
  Transistor #(.\type ("n")) transistor_7 (.in(1'b0), .out(pull_resistor_4_node), .gate(in_7));
  Transistor #(.\type ("n")) transistor_8 (.in(1'b0), .out(pull_resistor_4_node), .gate(_1077));
  Pull_Resistor #(.pull(1)) pull_resistor_5 (.node(pull_resistor_5_node));
  Transistor #(.\type ("n")) transistor_9 (.in(1'b0), .out(pull_resistor_5_node), .gate(_1077));
  Transistor #(.\type ("n")) transistor_10 (.in(1'b0), .out(pull_resistor_5_node), .gate(in_8));
  Pull_Resistor #(.pull(1)) pull_resistor_6 (.node(pull_resistor_6_node));
  Transistor #(.\type ("n")) transistor_11 (.in(1'b0), .out(pull_resistor_6_node), .gate(_1077));
  Transistor #(.\type ("n")) transistor_12 (.in(1'b0), .out(pull_resistor_6_node), .gate(in_9));
  Pull_Resistor #(.pull(1)) pull_resistor_7 (.node(pull_resistor_7_node));
  Transistor #(.\type ("n")) transistor_13 (.in(1'b0), .out(pull_resistor_7_node), .gate(_1077));
  Transistor #(.\type ("n")) transistor_14 (.in(1'b0), .out(pull_resistor_7_node), .gate(in_10));
  Pull_Resistor #(.pull(1)) pull_resistor_8 (.node(pull_resistor_8_node));
  Transistor #(.\type ("n")) transistor_15 (.in(1'b0), .out(pull_resistor_8_node), .gate(_1077));
  Transistor #(.\type ("n")) transistor_16 (.in(1'b0), .out(pull_resistor_8_node), .gate(in_11));
  Transistor #(.\type ("n")) transistor_17 (.in(pull_resistor_1_node), .out(transistor_17_out), .gate(_710));
  Transistor #(.\type ("n")) transistor_18 (.in(pull_resistor_2_node), .out(transistor_18_out), .gate(_710));
  Transistor #(.\type ("n")) transistor_19 (.in(pull_resistor_3_node), .out(transistor_19_out), .gate(_710));
  Transistor #(.\type ("n")) transistor_20 (.in(pull_resistor_4_node), .out(transistor_20_out), .gate(_710));
  Transistor #(.\type ("n")) transistor_21 (.in(pull_resistor_5_node), .out(transistor_21_out), .gate(_710));
  Transistor #(.\type ("n")) transistor_22 (.in(pull_resistor_6_node), .out(transistor_22_out), .gate(_710));
  Transistor #(.\type ("n")) transistor_23 (.in(pull_resistor_7_node), .out(transistor_23_out), .gate(_710));
  Transistor #(.\type ("n")) transistor_24 (.in(pull_resistor_8_node), .out(transistor_24_out), .gate(_710));
  Transistor #(.\type ("n")) transistor_25 (.in(transistor_17_out), .out(out_12), .gate(_724));
  Transistor #(.\type ("n")) transistor_26 (.in(transistor_18_out), .out(out_13), .gate(_724));
  Transistor #(.\type ("n")) transistor_27 (.in(transistor_19_out), .out(out_14), .gate(_724));
  Transistor #(.\type ("n")) transistor_28 (.in(transistor_20_out), .out(out_15), .gate(_724));
  Transistor #(.\type ("n")) transistor_29 (.in(transistor_21_out), .out(out_16), .gate(_724));
  Transistor #(.\type ("n")) transistor_30 (.in(transistor_22_out), .out(out_17), .gate(_724));
  Transistor #(.\type ("n")) transistor_31 (.in(transistor_23_out), .out(out_18), .gate(_724));
  Transistor #(.\type ("n")) transistor_32 (.in(transistor_24_out), .out(out_19), .gate(_724));
endmodule

module Instruction_Register (
  input  in_1,
  input  in_2,
  input  in_3,
  input  in_4,
  input  in_5,
  input  in_6,
  input  in_7,
  input  in_8,
  input  in_9,
  output out_10,
  output out_11,
  output out_12,
  output out_13,
  output out_14,
  output out_15,
  output out_16,
  output out_17,
  output out_18,
  output out_19,
  output out_20,
  output out_21,
  output out_22,
  output out_23,
  output out_24,
  output out_25
);

  wire register_1_q, register_2_q, register_3_q, register_4_q, register_5_q, register_6_q, register_7_q,
       register_8_q;

  Register #(.width(1), .trigger("high")) register_1 (.D(in_2), .Q(register_1_q), .clk(1'b1));  // open: en, clr
  Register #(.width(1), .trigger("high")) register_2 (.D(in_3), .Q(register_2_q), .clk(1'b1));  // open: en, clr
  Register #(.width(1), .trigger("high")) register_3 (.D(in_4), .Q(register_3_q), .clk(1'b1));  // open: en, clr
  Register #(.width(1), .trigger("high")) register_4 (.D(in_5), .Q(register_4_q), .clk(1'b1));  // open: en, clr
  Register #(.width(1), .trigger("high")) register_5 (.D(in_6), .Q(register_5_q), .clk(1'b1));  // open: en, clr
  Register #(.width(1), .trigger("high")) register_6 (.D(in_7), .Q(register_6_q), .clk(1'b1));  // open: en, clr
  Register #(.width(1), .trigger("high")) register_7 (.D(in_8), .Q(register_7_q), .clk(1'b1));  // open: en, clr
  Register #(.width(1), .trigger("high")) register_8 (.D(in_9), .Q(register_8_q), .clk(1'b1));  // open: en, clr
  Transistor #(.\type ("n")) transistor_1 (.in(1'b0), .out(out_10), .gate(register_1_q));
  Pull_Resistor #(.pull(1)) pull_resistor_1 (.node(out_10));
  Transistor #(.\type ("n")) transistor_2 (.in(out_11), .out(in_2), .gate(in_1));
  Transistor #(.\type ("n")) transistor_3 (.in(1'b0), .out(out_12), .gate(register_2_q));
  Pull_Resistor #(.pull(1)) pull_resistor_2 (.node(out_12));
  Transistor #(.\type ("n")) transistor_4 (.in(out_13), .out(in_3), .gate(in_1));
  Transistor #(.\type ("n")) transistor_5 (.in(1'b0), .out(out_14), .gate(register_3_q));
  Pull_Resistor #(.pull(1)) pull_resistor_3 (.node(out_14));
  Transistor #(.\type ("n")) transistor_6 (.in(out_15), .out(in_4), .gate(in_1));
  Pull_Resistor #(.pull(1)) pull_resistor_4 (.node(out_16));
  Transistor #(.\type ("n")) transistor_7 (.in(1'b0), .out(out_16), .gate(register_4_q));
  Transistor #(.\type ("n")) transistor_8 (.in(out_17), .out(in_5), .gate(in_1));
  Pull_Resistor #(.pull(1)) pull_resistor_5 (.node(out_18));
  Transistor #(.\type ("n")) transistor_9 (.in(1'b0), .out(out_18), .gate(register_5_q));
  Transistor #(.\type ("n")) transistor_10 (.in(out_19), .out(in_6), .gate(in_1));
  Transistor #(.\type ("n")) transistor_11 (.in(1'b0), .out(out_20), .gate(register_6_q));
  Pull_Resistor #(.pull(1)) pull_resistor_6 (.node(out_20));
  Transistor #(.\type ("n")) transistor_12 (.in(out_21), .out(in_7), .gate(in_1));
  Transistor #(.\type ("n")) transistor_13 (.in(1'b0), .out(out_22), .gate(register_7_q));
  Pull_Resistor #(.pull(1)) pull_resistor_7 (.node(out_22));
  Transistor #(.\type ("n")) transistor_14 (.in(out_23), .out(in_8), .gate(in_1));
  Pull_Resistor #(.pull(1)) pull_resistor_8 (.node(out_24));
  Transistor #(.\type ("n")) transistor_15 (.in(1'b0), .out(out_24), .gate(register_8_q));
  Transistor #(.\type ("n")) transistor_16 (.in(out_25), .out(in_9), .gate(in_1));
  Transistor #(.\type ("n")) transistor_17 (.in(1'b0), .out(out_11), .gate(out_10));
  Pull_Resistor #(.pull(1)) pull_resistor_9 (.node(out_11));
  Transistor #(.\type ("n")) transistor_18 (.in(1'b0), .out(out_13), .gate(out_12));
  Pull_Resistor #(.pull(1)) pull_resistor_10 (.node(out_13));
  Pull_Resistor #(.pull(1)) pull_resistor_11 (.node(out_15));
  Transistor #(.\type ("n")) transistor_19 (.in(1'b0), .out(out_15), .gate(out_14));
  Transistor #(.\type ("n")) transistor_20 (.in(1'b0), .out(out_17), .gate(out_16));
  Pull_Resistor #(.pull(1)) pull_resistor_12 (.node(out_17));
  Pull_Resistor #(.pull(1)) pull_resistor_13 (.node(out_19));
  Transistor #(.\type ("n")) transistor_21 (.in(1'b0), .out(out_19), .gate(out_18));
  Transistor #(.\type ("n")) transistor_22 (.in(1'b0), .out(out_21), .gate(out_20));
  Pull_Resistor #(.pull(1)) pull_resistor_14 (.node(out_21));
  Transistor #(.\type ("n")) transistor_23 (.in(1'b0), .out(out_23), .gate(out_22));
  Pull_Resistor #(.pull(1)) pull_resistor_15 (.node(out_23));
  Pull_Resistor #(.pull(1)) pull_resistor_16 (.node(out_25));
  Transistor #(.\type ("n")) transistor_24 (.in(1'b0), .out(out_25), .gate(out_24));
endmodule

module ADL_Precharge_Mosfets (
  input  _943,
  output out_2,
  output out_3,
  output out_4,
  output out_5,
  output out_6,
  output out_7,
  output out_8,
  output out_9
);

  Transistor #(.\type ("n")) transistor_1 (.in(1'b1), .out(out_2), .gate(_943));
  Transistor #(.\type ("n")) transistor_2 (.in(1'b1), .out(out_3), .gate(_943));
  Transistor #(.\type ("n")) transistor_3 (.in(1'b1), .out(out_4), .gate(_943));
  Transistor #(.\type ("n")) transistor_4 (.in(1'b1), .out(out_5), .gate(_943));
  Transistor #(.\type ("n")) transistor_5 (.in(1'b1), .out(out_6), .gate(_943));
  Transistor #(.\type ("n")) transistor_6 (.in(1'b1), .out(out_7), .gate(_943));
  Transistor #(.\type ("n")) transistor_7 (.in(1'b1), .out(out_8), .gate(_943));
  Transistor #(.\type ("n")) transistor_8 (.in(1'b1), .out(out_9), .gate(_943));
endmodule

module ABL_Register (
  input  in_1,
  input  in_2,
  input  in_3,
  input  in_4,
  input  in_5,
  input  in_6,
  input  in_7,
  input  in_8,
  input  in_9,
  input  in_10,
  input  in_11,
  output _268,
  output _268_2,
  output _268_3,
  output _268_4,
  output _268_5,
  output _268_6,
  output _268_7,
  output _268_8
);

  wire pull_resistor_1_node, pull_resistor_2_node, pull_resistor_5_node, pull_resistor_10_node,
       pull_resistor_11_node, pull_resistor_15_node, pull_resistor_17_node, pull_resistor_22_node,
       pull_resistor_24_node, register_1_q, register_2_q, register_3_q, register_4_q, register_5_q,
       register_6_q, register_7_q, register_8_q, transistor_3_out, transistor_4_out, transistor_6_out,
       transistor_7_out, transistor_8_out, transistor_9_out, transistor_10_out, transistor_11_out,
       transistor_12_out, transistor_13_out, transistor_14_out, transistor_15_out, transistor_16_out,
       transistor_17_out, transistor_18_out, transistor_19_out, transistor_20_out, transistor_21_out,
       transistor_22_out, transistor_23_out, transistor_24_out, transistor_25_out, transistor_31_out,
       transistor_33_out, transistor_35_out, transistor_39_out, transistor_42_out, transistor_43_out,
       transistor_44_out, transistor_45_out, transistor_47_out, transistor_49_out, transistor_51_out,
       transistor_53_out, transistor_55_out, transistor_57_out, transistor_59_out, transistor_61_out,
       transistor_63_out, transistor_65_out, transistor_67_out, transistor_69_out, transistor_71_out,
       transistor_73_out, transistor_75_out, transistor_77_out, transistor_79_out;

  Pull_Resistor #(.pull(1)) pull_resistor_1 (.node(pull_resistor_1_node));
  Transistor #(.\type ("n")) transistor_1 (.in(1'b0), .out(pull_resistor_1_node), .gate(in_4));
  Pull_Resistor #(.pull(1)) pull_resistor_2 (.node(pull_resistor_2_node));
  Transistor #(.\type ("n")) transistor_2 (.in(1'b0), .out(pull_resistor_2_node), .gate(in_5));
  Transistor #(.\type ("n")) transistor_3 (.in(1'b0), .out(transistor_3_out), .gate(in_6));
  Pull_Resistor #(.pull(1)) pull_resistor_3 (.node(transistor_3_out));
  Transistor #(.\type ("n")) transistor_4 (.in(1'b0), .out(transistor_4_out), .gate(in_7));
  Pull_Resistor #(.pull(1)) pull_resistor_4 (.node(transistor_4_out));
  Pull_Resistor #(.pull(1)) pull_resistor_5 (.node(pull_resistor_5_node));
  Transistor #(.\type ("n")) transistor_5 (.in(1'b0), .out(pull_resistor_5_node), .gate(in_8));
  Transistor #(.\type ("n")) transistor_6 (.in(1'b0), .out(transistor_6_out), .gate(in_9));
  Pull_Resistor #(.pull(1)) pull_resistor_6 (.node(transistor_6_out));
  Transistor #(.\type ("n")) transistor_7 (.in(1'b0), .out(transistor_7_out), .gate(in_10));
  Pull_Resistor #(.pull(1)) pull_resistor_7 (.node(transistor_7_out));
  Transistor #(.\type ("n")) transistor_8 (.in(1'b0), .out(transistor_8_out), .gate(in_11));
  Pull_Resistor #(.pull(1)) pull_resistor_8 (.node(transistor_8_out));
  Transistor #(.\type ("n")) transistor_9 (.in(pull_resistor_1_node), .out(transistor_9_out), .gate(in_1));
  Transistor #(.\type ("n")) transistor_10 (.in(pull_resistor_2_node), .out(transistor_10_out), .gate(in_1));
  Transistor #(.\type ("n")) transistor_11 (.in(transistor_3_out), .out(transistor_11_out), .gate(in_1));
  Transistor #(.\type ("n")) transistor_12 (.in(transistor_4_out), .out(transistor_12_out), .gate(in_1));
  Transistor #(.\type ("n")) transistor_13 (.in(pull_resistor_5_node), .out(transistor_13_out), .gate(in_1));
  Transistor #(.\type ("n")) transistor_14 (.in(transistor_6_out), .out(transistor_14_out), .gate(in_1));
  Transistor #(.\type ("n")) transistor_15 (.in(transistor_7_out), .out(transistor_15_out), .gate(in_1));
  Transistor #(.\type ("n")) transistor_16 (.in(transistor_8_out), .out(transistor_16_out), .gate(in_1));
  Transistor #(.\type ("n")) transistor_17 (.in(transistor_9_out), .out(transistor_17_out), .gate(in_2));
  Transistor #(.\type ("n")) transistor_18 (.in(transistor_10_out), .out(transistor_18_out), .gate(in_2));
  Transistor #(.\type ("n")) transistor_19 (.in(transistor_11_out), .out(transistor_19_out), .gate(in_2));
  Transistor #(.\type ("n")) transistor_20 (.in(transistor_12_out), .out(transistor_20_out), .gate(in_2));
  Transistor #(.\type ("n")) transistor_21 (.in(transistor_13_out), .out(transistor_21_out), .gate(in_2));
  Transistor #(.\type ("n")) transistor_22 (.in(transistor_14_out), .out(transistor_22_out), .gate(in_2));
  Transistor #(.\type ("n")) transistor_23 (.in(transistor_15_out), .out(transistor_23_out), .gate(in_2));
  Transistor #(.\type ("n")) transistor_24 (.in(transistor_16_out), .out(transistor_24_out), .gate(in_2));
  Register #(.width(1), .trigger("high")) register_1 (
    .D(transistor_17_out), .Q(register_1_q), .clk(1'b1));  // open: en, clr
  Register #(.width(1), .trigger("high")) register_2 (
    .D(transistor_18_out), .Q(register_2_q), .clk(1'b1));  // open: en, clr
  Register #(.width(1), .trigger("high")) register_3 (
    .D(transistor_19_out), .Q(register_3_q), .clk(1'b1));  // open: en, clr
  Register #(.width(1), .trigger("high")) register_4 (
    .D(transistor_20_out), .Q(register_4_q), .clk(1'b1));  // open: en, clr
  Register #(.width(1), .trigger("high")) register_5 (
    .D(transistor_21_out), .Q(register_5_q), .clk(1'b1));  // open: en, clr
  Register #(.width(1), .trigger("high")) register_6 (
    .D(transistor_22_out), .Q(register_6_q), .clk(1'b1));  // open: en, clr
  Register #(.width(1), .trigger("high")) register_7 (
    .D(transistor_23_out), .Q(register_7_q), .clk(1'b1));  // open: en, clr
  Register #(.width(1), .trigger("high")) register_8 (
    .D(transistor_24_out), .Q(register_8_q), .clk(1'b1));  // open: en, clr
  Transistor #(.\type ("n")) transistor_25 (.in(1'b0), .out(transistor_25_out), .gate(register_1_q));
  Pull_Resistor #(.pull(1)) pull_resistor_9 (.node(transistor_25_out));
  Transistor #(.\type ("n")) transistor_26 (.in(transistor_51_out), .out(transistor_17_out), .gate(in_3));
  Pull_Resistor #(.pull(1)) pull_resistor_10 (.node(pull_resistor_10_node));
  Transistor #(.\type ("n")) transistor_27 (.in(1'b0), .out(pull_resistor_10_node), .gate(register_2_q));
  Transistor #(.\type ("n")) transistor_28 (.in(transistor_55_out), .out(transistor_18_out), .gate(in_3));
  Pull_Resistor #(.pull(1)) pull_resistor_11 (.node(pull_resistor_11_node));
  Transistor #(.\type ("n")) transistor_29 (.in(1'b0), .out(pull_resistor_11_node), .gate(register_3_q));
  Transistor #(.\type ("n")) transistor_30 (.in(transistor_59_out), .out(transistor_19_out), .gate(in_3));
  Transistor #(.\type ("n")) transistor_31 (.in(1'b0), .out(transistor_31_out), .gate(register_4_q));
  Pull_Resistor #(.pull(1)) pull_resistor_12 (.node(transistor_31_out));
  Transistor #(.\type ("n")) transistor_32 (.in(transistor_63_out), .out(transistor_20_out), .gate(in_3));
  Transistor #(.\type ("n")) transistor_33 (.in(1'b0), .out(transistor_33_out), .gate(register_5_q));
  Pull_Resistor #(.pull(1)) pull_resistor_13 (.node(transistor_33_out));
  Transistor #(.\type ("n")) transistor_34 (.in(transistor_67_out), .out(transistor_21_out), .gate(in_3));
  Transistor #(.\type ("n")) transistor_35 (.in(1'b0), .out(transistor_35_out), .gate(register_6_q));
  Pull_Resistor #(.pull(1)) pull_resistor_14 (.node(transistor_35_out));
  Transistor #(.\type ("n")) transistor_36 (.in(transistor_71_out), .out(transistor_22_out), .gate(in_3));
  Pull_Resistor #(.pull(1)) pull_resistor_15 (.node(pull_resistor_15_node));
  Transistor #(.\type ("n")) transistor_37 (.in(1'b0), .out(pull_resistor_15_node), .gate(register_7_q));
  Transistor #(.\type ("n")) transistor_38 (.in(transistor_75_out), .out(transistor_23_out), .gate(in_3));
  Transistor #(.\type ("n")) transistor_39 (.in(1'b0), .out(transistor_39_out), .gate(register_8_q));
  Pull_Resistor #(.pull(1)) pull_resistor_16 (.node(transistor_39_out));
  Transistor #(.\type ("n")) transistor_40 (.in(transistor_79_out), .out(transistor_24_out), .gate(in_3));
  Pull_Resistor #(.pull(1)) pull_resistor_17 (.node(pull_resistor_17_node));
  Transistor #(.\type ("n")) transistor_41 (.in(1'b0), .out(pull_resistor_17_node), .gate(transistor_25_out));
  Transistor #(.\type ("n")) transistor_42 (.in(1'b0), .out(transistor_42_out), .gate(pull_resistor_10_node));
  Pull_Resistor #(.pull(1)) pull_resistor_18 (.node(transistor_42_out));
  Transistor #(.\type ("n")) transistor_43 (.in(1'b0), .out(transistor_43_out), .gate(pull_resistor_11_node));
  Pull_Resistor #(.pull(1)) pull_resistor_19 (.node(transistor_43_out));
  Transistor #(.\type ("n")) transistor_44 (.in(1'b0), .out(transistor_44_out), .gate(transistor_31_out));
  Pull_Resistor #(.pull(1)) pull_resistor_20 (.node(transistor_44_out));
  Transistor #(.\type ("n")) transistor_45 (.in(1'b0), .out(transistor_45_out), .gate(transistor_33_out));
  Pull_Resistor #(.pull(1)) pull_resistor_21 (.node(transistor_45_out));
  Pull_Resistor #(.pull(1)) pull_resistor_22 (.node(pull_resistor_22_node));
  Transistor #(.\type ("n")) transistor_46 (.in(1'b0), .out(pull_resistor_22_node), .gate(transistor_35_out));
  Transistor #(.\type ("n")) transistor_47 (.in(1'b0), .out(transistor_47_out), .gate(pull_resistor_15_node));
  Pull_Resistor #(.pull(1)) pull_resistor_23 (.node(transistor_47_out));
  Pull_Resistor #(.pull(1)) pull_resistor_24 (.node(pull_resistor_24_node));
  Transistor #(.\type ("n")) transistor_48 (.in(1'b0), .out(pull_resistor_24_node), .gate(transistor_39_out));
  Transistor #(.\type ("n")) transistor_49 (.in(1'b1), .out(transistor_49_out), .gate(transistor_25_out));
  Transistor #(.\type ("n")) transistor_50 (.in(1'b0), .out(transistor_49_out), .gate(pull_resistor_17_node));
  Transistor #(.\type ("n")) transistor_51 (.in(1'b1), .out(transistor_51_out), .gate(pull_resistor_17_node));
  Transistor #(.\type ("n")) transistor_52 (.in(1'b0), .out(transistor_51_out), .gate(transistor_25_out));
  Transistor #(.\type ("n")) transistor_53 (.in(1'b1), .out(transistor_53_out), .gate(pull_resistor_10_node));
  Transistor #(.\type ("n")) transistor_54 (.in(1'b0), .out(transistor_53_out), .gate(transistor_42_out));
  Transistor #(.\type ("n")) transistor_55 (.in(1'b1), .out(transistor_55_out), .gate(transistor_42_out));
  Transistor #(.\type ("n")) transistor_56 (.in(1'b0), .out(transistor_55_out), .gate(pull_resistor_10_node));
  Transistor #(.\type ("n")) transistor_57 (.in(1'b1), .out(transistor_57_out), .gate(pull_resistor_11_node));
  Transistor #(.\type ("n")) transistor_58 (.in(1'b0), .out(transistor_57_out), .gate(transistor_43_out));
  Transistor #(.\type ("n")) transistor_59 (.in(1'b1), .out(transistor_59_out), .gate(transistor_43_out));
  Transistor #(.\type ("n")) transistor_60 (.in(1'b0), .out(transistor_59_out), .gate(pull_resistor_11_node));
  Transistor #(.\type ("n")) transistor_61 (.in(1'b1), .out(transistor_61_out), .gate(transistor_31_out));
  Transistor #(.\type ("n")) transistor_62 (.in(1'b0), .out(transistor_61_out), .gate(transistor_44_out));
  Transistor #(.\type ("n")) transistor_63 (.in(1'b1), .out(transistor_63_out), .gate(transistor_44_out));
  Transistor #(.\type ("n")) transistor_64 (.in(1'b0), .out(transistor_63_out), .gate(transistor_31_out));
  Transistor #(.\type ("n")) transistor_65 (.in(1'b1), .out(transistor_65_out), .gate(transistor_33_out));
  Transistor #(.\type ("n")) transistor_66 (.in(1'b0), .out(transistor_65_out), .gate(transistor_45_out));
  Transistor #(.\type ("n")) transistor_67 (.in(1'b1), .out(transistor_67_out), .gate(transistor_45_out));
  Transistor #(.\type ("n")) transistor_68 (.in(1'b0), .out(transistor_67_out), .gate(transistor_33_out));
  Transistor #(.\type ("n")) transistor_69 (.in(1'b1), .out(transistor_69_out), .gate(transistor_35_out));
  Transistor #(.\type ("n")) transistor_70 (.in(1'b0), .out(transistor_69_out), .gate(pull_resistor_22_node));
  Transistor #(.\type ("n")) transistor_71 (.in(1'b1), .out(transistor_71_out), .gate(pull_resistor_22_node));
  Transistor #(.\type ("n")) transistor_72 (.in(1'b0), .out(transistor_71_out), .gate(transistor_35_out));
  Transistor #(.\type ("n")) transistor_73 (.in(1'b1), .out(transistor_73_out), .gate(pull_resistor_15_node));
  Transistor #(.\type ("n")) transistor_74 (.in(1'b0), .out(transistor_73_out), .gate(transistor_47_out));
  Transistor #(.\type ("n")) transistor_75 (.in(1'b1), .out(transistor_75_out), .gate(transistor_47_out));
  Transistor #(.\type ("n")) transistor_76 (.in(1'b0), .out(transistor_75_out), .gate(pull_resistor_15_node));
  Transistor #(.\type ("n")) transistor_77 (.in(1'b1), .out(transistor_77_out), .gate(transistor_39_out));
  Transistor #(.\type ("n")) transistor_78 (.in(1'b0), .out(transistor_77_out), .gate(pull_resistor_24_node));
  Transistor #(.\type ("n")) transistor_79 (.in(1'b1), .out(transistor_79_out), .gate(pull_resistor_24_node));
  Transistor #(.\type ("n")) transistor_80 (.in(1'b0), .out(transistor_79_out), .gate(transistor_39_out));
  Transistor #(.\type ("n")) transistor_81 (.in(1'b1), .out(_268), .gate(transistor_49_out));
  Transistor #(.\type ("n")) transistor_82 (.in(1'b1), .out(_268), .gate(transistor_49_out));
  Transistor #(.\type ("n")) transistor_83 (.in(1'b1), .out(_268_2), .gate(transistor_53_out));
  Transistor #(.\type ("n")) transistor_84 (.in(1'b1), .out(_268_2), .gate(transistor_53_out));
  Transistor #(.\type ("n")) transistor_85 (.in(1'b1), .out(_268_3), .gate(transistor_57_out));
  Transistor #(.\type ("n")) transistor_86 (.in(1'b1), .out(_268_3), .gate(transistor_57_out));
  Transistor #(.\type ("n")) transistor_87 (.in(1'b1), .out(_268_4), .gate(transistor_61_out));
  Transistor #(.\type ("n")) transistor_88 (.in(1'b1), .out(_268_4), .gate(transistor_61_out));
  Transistor #(.\type ("n")) transistor_89 (.in(1'b1), .out(_268_5), .gate(transistor_65_out));
  Transistor #(.\type ("n")) transistor_90 (.in(1'b1), .out(_268_5), .gate(transistor_65_out));
  Transistor #(.\type ("n")) transistor_91 (.in(1'b1), .out(_268_6), .gate(transistor_69_out));
  Transistor #(.\type ("n")) transistor_92 (.in(1'b1), .out(_268_6), .gate(transistor_69_out));
  Transistor #(.\type ("n")) transistor_93 (.in(1'b1), .out(_268_7), .gate(transistor_73_out));
  Transistor #(.\type ("n")) transistor_94 (.in(1'b1), .out(_268_7), .gate(transistor_73_out));
  Transistor #(.\type ("n")) transistor_95 (.in(1'b1), .out(_268_8), .gate(transistor_77_out));
  Transistor #(.\type ("n")) transistor_96 (.in(1'b1), .out(_268_8), .gate(transistor_77_out));
  Transistor #(.\type ("n")) transistor_97 (.in(1'b1), .out(_268), .gate(transistor_49_out));
  Transistor #(.\type ("n")) transistor_98 (.in(1'b1), .out(_268), .gate(transistor_49_out));
  Transistor #(.\type ("n")) transistor_99 (.in(1'b0), .out(_268), .gate(transistor_51_out));
  Transistor #(.\type ("n")) transistor_100 (.in(1'b0), .out(_268), .gate(transistor_51_out));
  Transistor #(.\type ("n")) transistor_101 (.in(1'b1), .out(_268_2), .gate(transistor_53_out));
  Transistor #(.\type ("n")) transistor_102 (.in(1'b1), .out(_268_2), .gate(transistor_53_out));
  Transistor #(.\type ("n")) transistor_103 (.in(1'b0), .out(_268_2), .gate(transistor_55_out));
  Transistor #(.\type ("n")) transistor_104 (.in(1'b0), .out(_268_2), .gate(transistor_55_out));
  Transistor #(.\type ("n")) transistor_105 (.in(1'b1), .out(_268_3), .gate(transistor_57_out));
  Transistor #(.\type ("n")) transistor_106 (.in(1'b1), .out(_268_3), .gate(transistor_57_out));
  Transistor #(.\type ("n")) transistor_107 (.in(1'b0), .out(_268_3), .gate(transistor_59_out));
  Transistor #(.\type ("n")) transistor_108 (.in(1'b0), .out(_268_3), .gate(transistor_59_out));
  Transistor #(.\type ("n")) transistor_109 (.in(1'b1), .out(_268_4), .gate(transistor_61_out));
  Transistor #(.\type ("n")) transistor_110 (.in(1'b1), .out(_268_4), .gate(transistor_61_out));
  Transistor #(.\type ("n")) transistor_111 (.in(1'b0), .out(_268_4), .gate(transistor_63_out));
  Transistor #(.\type ("n")) transistor_112 (.in(1'b0), .out(_268_4), .gate(transistor_63_out));
  Transistor #(.\type ("n")) transistor_113 (.in(1'b1), .out(_268_5), .gate(transistor_65_out));
  Transistor #(.\type ("n")) transistor_114 (.in(1'b1), .out(_268_5), .gate(transistor_65_out));
  Transistor #(.\type ("n")) transistor_115 (.in(1'b0), .out(_268_5), .gate(transistor_67_out));
  Transistor #(.\type ("n")) transistor_116 (.in(1'b0), .out(_268_5), .gate(transistor_67_out));
  Transistor #(.\type ("n")) transistor_117 (.in(1'b1), .out(_268_6), .gate(transistor_69_out));
  Transistor #(.\type ("n")) transistor_118 (.in(1'b1), .out(_268_6), .gate(transistor_69_out));
  Transistor #(.\type ("n")) transistor_119 (.in(1'b0), .out(_268_6), .gate(transistor_71_out));
  Transistor #(.\type ("n")) transistor_120 (.in(1'b0), .out(_268_6), .gate(transistor_71_out));
  Transistor #(.\type ("n")) transistor_121 (.in(1'b1), .out(_268_7), .gate(transistor_73_out));
  Transistor #(.\type ("n")) transistor_122 (.in(1'b1), .out(_268_7), .gate(transistor_73_out));
  Transistor #(.\type ("n")) transistor_123 (.in(1'b0), .out(_268_7), .gate(transistor_75_out));
  Transistor #(.\type ("n")) transistor_124 (.in(1'b0), .out(_268_7), .gate(transistor_75_out));
  Transistor #(.\type ("n")) transistor_125 (.in(1'b1), .out(_268_8), .gate(transistor_77_out));
  Transistor #(.\type ("n")) transistor_126 (.in(1'b1), .out(_268_8), .gate(transistor_77_out));
  Transistor #(.\type ("n")) transistor_127 (.in(1'b0), .out(_268_8), .gate(transistor_79_out));
  Transistor #(.\type ("n")) transistor_128 (.in(1'b0), .out(_268_8), .gate(transistor_79_out));
  Transistor #(.\type ("n")) transistor_129 (.in(1'b1), .out(_268), .gate(transistor_49_out));
  Transistor #(.\type ("n")) transistor_130 (.in(1'b0), .out(_268), .gate(transistor_51_out));
  Transistor #(.\type ("n")) transistor_131 (.in(1'b1), .out(_268_2), .gate(transistor_53_out));
  Transistor #(.\type ("n")) transistor_132 (.in(1'b0), .out(_268_2), .gate(transistor_55_out));
  Transistor #(.\type ("n")) transistor_133 (.in(1'b1), .out(_268_3), .gate(transistor_57_out));
  Transistor #(.\type ("n")) transistor_134 (.in(1'b0), .out(_268_3), .gate(transistor_59_out));
  Transistor #(.\type ("n")) transistor_135 (.in(1'b1), .out(_268_4), .gate(transistor_61_out));
  Transistor #(.\type ("n")) transistor_136 (.in(1'b0), .out(_268_4), .gate(transistor_63_out));
  Transistor #(.\type ("n")) transistor_137 (.in(1'b1), .out(_268_5), .gate(transistor_65_out));
  Transistor #(.\type ("n")) transistor_138 (.in(1'b0), .out(_268_5), .gate(transistor_67_out));
  Transistor #(.\type ("n")) transistor_139 (.in(1'b1), .out(_268_6), .gate(transistor_69_out));
  Transistor #(.\type ("n")) transistor_140 (.in(1'b0), .out(_268_6), .gate(transistor_71_out));
  Transistor #(.\type ("n")) transistor_141 (.in(1'b1), .out(_268_7), .gate(transistor_73_out));
  Transistor #(.\type ("n")) transistor_142 (.in(1'b0), .out(_268_7), .gate(transistor_75_out));
  Transistor #(.\type ("n")) transistor_143 (.in(1'b1), .out(_268_8), .gate(transistor_77_out));
  Transistor #(.\type ("n")) transistor_144 (.in(1'b0), .out(_268_8), .gate(transistor_79_out));

  // Notes on the sheet:
  //   153
  //   153
  //   153
  //   153
  //   153
  //   153
  //   153
  //   153
  //   1096
  //   1660
  //   1096
  //   1660
  //   1096
  //   1660
  //   1096
  //   1660
  //   1096
  //   1660
  //   1096
  //   1660
  //   1096
  //   1660
  //   1096
  //   1660
  //   855
  //   1100
  //   855
  //   1100
  //   855
  //   1100
  //   855
  //   1100
  //   855
  //   1100
  //   855
  //   1100
  //   855
  //   1100
  //   855
  //   1100
endmodule

module ADH_Precharge_Mosfets (
  input  _943,
  output out_2,
  output out_3,
  output out_4,
  output out_5,
  output out_6,
  output out_7,
  output out_8,
  output out_9
);

  Transistor #(.\type ("n")) transistor_1 (.in(1'b1), .out(out_2), .gate(_943));
  Transistor #(.\type ("n")) transistor_2 (.in(1'b1), .out(out_3), .gate(_943));
  Transistor #(.\type ("n")) transistor_3 (.in(1'b1), .out(out_4), .gate(_943));
  Transistor #(.\type ("n")) transistor_4 (.in(1'b1), .out(out_5), .gate(_943));
  Transistor #(.\type ("n")) transistor_5 (.in(1'b1), .out(out_6), .gate(_943));
  Transistor #(.\type ("n")) transistor_6 (.in(1'b1), .out(out_7), .gate(_943));
  Transistor #(.\type ("n")) transistor_7 (.in(1'b1), .out(out_8), .gate(_943));
  Transistor #(.\type ("n")) transistor_8 (.in(1'b1), .out(out_9), .gate(_943));
endmodule

module ADH_Open_Drain_Mosfets (
  input  in_1,
  input  in_2,
  output out_3,
  output out_4,
  output out_5,
  output out_6,
  output out_7,
  output out_8,
  output out_9,
  output out_10
);

  Transistor #(.\type ("n")) transistor_1 (.in(1'b0), .out(out_3), .gate(in_1));
  Transistor #(.\type ("n")) transistor_2 (.in(1'b0), .out(out_4), .gate(in_2));
  Transistor #(.\type ("n")) transistor_3 (.in(1'b0), .out(out_5), .gate(in_2));
  Transistor #(.\type ("n")) transistor_4 (.in(1'b0), .out(out_6), .gate(in_2));
  Transistor #(.\type ("n")) transistor_5 (.in(1'b0), .out(out_7), .gate(in_2));
  Transistor #(.\type ("n")) transistor_6 (.in(1'b0), .out(out_8), .gate(in_2));
  Transistor #(.\type ("n")) transistor_7 (.in(1'b0), .out(out_9), .gate(in_2));
  Transistor #(.\type ("n")) transistor_8 (.in(1'b0), .out(out_10), .gate(in_2));
endmodule
module ABH_Register (
  input  in_1,
  input  in_2,
  input  in_3,
  input  in_4,
  input  in_5,
  input  in_6,
  input  in_7,
  input  in_8,
  input  in_9,
  input  in_10,
  input  in_11,
  output _268,
  output _268_2,
  output _268_3,
  output _268_4,
  output _268_5,
  output _268_6,
  output _268_7,
  output _268_8
);

  wire pull_resistor_4_node, pull_resistor_5_node, pull_resistor_6_node, pull_resistor_7_node,
       pull_resistor_8_node, pull_resistor_9_node, pull_resistor_10_node, pull_resistor_12_node,
       pull_resistor_14_node, pull_resistor_15_node, pull_resistor_16_node, pull_resistor_17_node,
       pull_resistor_18_node, pull_resistor_19_node, pull_resistor_20_node, pull_resistor_21_node,
       register_1_q, register_2_q, register_3_q, register_4_q, register_5_q, register_6_q, register_7_q,
       register_8_q, transistor_1_out, transistor_2_out, transistor_3_out, transistor_9_out,
       transistor_10_out, transistor_11_out, transistor_12_out, transistor_13_out, transistor_14_out,
       transistor_15_out, transistor_16_out, transistor_17_out, transistor_18_out, transistor_19_out,
       transistor_20_out, transistor_21_out, transistor_22_out, transistor_23_out, transistor_24_out,
       transistor_29_out, transistor_33_out, transistor_46_out, transistor_47_out, transistor_48_out,
       transistor_49_out, transistor_51_out, transistor_53_out, transistor_55_out, transistor_57_out,
       transistor_59_out, transistor_61_out, transistor_63_out, transistor_65_out, transistor_67_out,
       transistor_69_out, transistor_71_out, transistor_73_out, transistor_75_out, transistor_77_out,
       transistor_79_out;

  Transistor #(.\type ("n")) transistor_1 (.in(1'b0), .out(transistor_1_out), .gate(in_4));
  Pull_Resistor #(.pull(1)) pull_resistor_1 (.node(transistor_1_out));
  Transistor #(.\type ("n")) transistor_2 (.in(1'b0), .out(transistor_2_out), .gate(in_5));
  Pull_Resistor #(.pull(1)) pull_resistor_2 (.node(transistor_2_out));
  Transistor #(.\type ("n")) transistor_3 (.in(1'b0), .out(transistor_3_out), .gate(in_6));
  Pull_Resistor #(.pull(1)) pull_resistor_3 (.node(transistor_3_out));
  Pull_Resistor #(.pull(1)) pull_resistor_4 (.node(pull_resistor_4_node));
  Transistor #(.\type ("n")) transistor_4 (.in(1'b0), .out(pull_resistor_4_node), .gate(in_7));
  Pull_Resistor #(.pull(1)) pull_resistor_5 (.node(pull_resistor_5_node));
  Transistor #(.\type ("n")) transistor_5 (.in(1'b0), .out(pull_resistor_5_node), .gate(in_8));
  Pull_Resistor #(.pull(1)) pull_resistor_6 (.node(pull_resistor_6_node));
  Transistor #(.\type ("n")) transistor_6 (.in(1'b0), .out(pull_resistor_6_node), .gate(in_9));
  Pull_Resistor #(.pull(1)) pull_resistor_7 (.node(pull_resistor_7_node));
  Transistor #(.\type ("n")) transistor_7 (.in(1'b0), .out(pull_resistor_7_node), .gate(in_10));
  Pull_Resistor #(.pull(1)) pull_resistor_8 (.node(pull_resistor_8_node));
  Transistor #(.\type ("n")) transistor_8 (.in(1'b0), .out(pull_resistor_8_node), .gate(in_11));
  Transistor #(.\type ("n")) transistor_9 (.in(transistor_1_out), .out(transistor_9_out), .gate(in_1));
  Transistor #(.\type ("n")) transistor_10 (.in(transistor_2_out), .out(transistor_10_out), .gate(in_1));
  Transistor #(.\type ("n")) transistor_11 (.in(transistor_3_out), .out(transistor_11_out), .gate(in_1));
  Transistor #(.\type ("n")) transistor_12 (.in(pull_resistor_4_node), .out(transistor_12_out), .gate(in_1));
  Transistor #(.\type ("n")) transistor_13 (.in(pull_resistor_5_node), .out(transistor_13_out), .gate(in_1));
  Transistor #(.\type ("n")) transistor_14 (.in(pull_resistor_6_node), .out(transistor_14_out), .gate(in_1));
  Transistor #(.\type ("n")) transistor_15 (.in(pull_resistor_7_node), .out(transistor_15_out), .gate(in_1));
  Transistor #(.\type ("n")) transistor_16 (.in(pull_resistor_8_node), .out(transistor_16_out), .gate(in_1));
  Transistor #(.\type ("n")) transistor_17 (.in(transistor_9_out), .out(transistor_17_out), .gate(in_2));
  Transistor #(.\type ("n")) transistor_18 (.in(transistor_10_out), .out(transistor_18_out), .gate(in_2));
  Transistor #(.\type ("n")) transistor_19 (.in(transistor_11_out), .out(transistor_19_out), .gate(in_2));
  Transistor #(.\type ("n")) transistor_20 (.in(transistor_12_out), .out(transistor_20_out), .gate(in_2));
  Transistor #(.\type ("n")) transistor_21 (.in(transistor_13_out), .out(transistor_21_out), .gate(in_2));
  Transistor #(.\type ("n")) transistor_22 (.in(transistor_14_out), .out(transistor_22_out), .gate(in_2));
  Transistor #(.\type ("n")) transistor_23 (.in(transistor_15_out), .out(transistor_23_out), .gate(in_2));
  Transistor #(.\type ("n")) transistor_24 (.in(transistor_16_out), .out(transistor_24_out), .gate(in_2));
  Register #(.width(1), .trigger("high")) register_1 (
    .D(transistor_17_out), .Q(register_1_q), .clk(1'b1));  // open: en, clr
  Register #(.width(1), .trigger("high")) register_2 (
    .D(transistor_18_out), .Q(register_2_q), .clk(1'b1));  // open: en, clr
  Register #(.width(1), .trigger("high")) register_3 (
    .D(transistor_19_out), .Q(register_3_q), .clk(1'b1));  // open: en, clr
  Register #(.width(1), .trigger("high")) register_4 (
    .D(transistor_20_out), .Q(register_4_q), .clk(1'b1));  // open: en, clr
  Register #(.width(1), .trigger("high")) register_5 (
    .D(transistor_21_out), .Q(register_5_q), .clk(1'b1));  // open: en, clr
  Register #(.width(1), .trigger("high")) register_6 (
    .D(transistor_22_out), .Q(register_6_q), .clk(1'b1));  // open: en, clr
  Register #(.width(1), .trigger("high")) register_7 (
    .D(transistor_23_out), .Q(register_7_q), .clk(1'b1));  // open: en, clr
  Register #(.width(1), .trigger("high")) register_8 (
    .D(transistor_24_out), .Q(register_8_q), .clk(1'b1));  // open: en, clr
  Pull_Resistor #(.pull(1)) pull_resistor_9 (.node(pull_resistor_9_node));
  Transistor #(.\type ("n")) transistor_25 (.in(1'b0), .out(pull_resistor_9_node), .gate(register_1_q));
  Transistor #(.\type ("n")) transistor_26 (.in(transistor_51_out), .out(transistor_17_out), .gate(in_3));
  Pull_Resistor #(.pull(1)) pull_resistor_10 (.node(pull_resistor_10_node));
  Transistor #(.\type ("n")) transistor_27 (.in(1'b0), .out(pull_resistor_10_node), .gate(register_2_q));
  Transistor #(.\type ("n")) transistor_28 (.in(transistor_55_out), .out(transistor_18_out), .gate(in_3));
  Transistor #(.\type ("n")) transistor_29 (.in(1'b0), .out(transistor_29_out), .gate(register_3_q));
  Pull_Resistor #(.pull(1)) pull_resistor_11 (.node(transistor_29_out));
  Transistor #(.\type ("n")) transistor_30 (.in(transistor_59_out), .out(transistor_19_out), .gate(in_3));
  Pull_Resistor #(.pull(1)) pull_resistor_12 (.node(pull_resistor_12_node));
  Transistor #(.\type ("n")) transistor_31 (.in(1'b0), .out(pull_resistor_12_node), .gate(register_4_q));
  Transistor #(.\type ("n")) transistor_32 (.in(transistor_63_out), .out(transistor_20_out), .gate(in_3));
  Transistor #(.\type ("n")) transistor_33 (.in(1'b0), .out(transistor_33_out), .gate(register_5_q));
  Pull_Resistor #(.pull(1)) pull_resistor_13 (.node(transistor_33_out));
  Transistor #(.\type ("n")) transistor_34 (.in(transistor_67_out), .out(transistor_21_out), .gate(in_3));
  Pull_Resistor #(.pull(1)) pull_resistor_14 (.node(pull_resistor_14_node));
  Transistor #(.\type ("n")) transistor_35 (.in(1'b0), .out(pull_resistor_14_node), .gate(register_6_q));
  Transistor #(.\type ("n")) transistor_36 (.in(transistor_71_out), .out(transistor_22_out), .gate(in_3));
  Pull_Resistor #(.pull(1)) pull_resistor_15 (.node(pull_resistor_15_node));
  Transistor #(.\type ("n")) transistor_37 (.in(1'b0), .out(pull_resistor_15_node), .gate(register_7_q));
  Transistor #(.\type ("n")) transistor_38 (.in(transistor_75_out), .out(transistor_23_out), .gate(in_3));
  Pull_Resistor #(.pull(1)) pull_resistor_16 (.node(pull_resistor_16_node));
  Transistor #(.\type ("n")) transistor_39 (.in(1'b0), .out(pull_resistor_16_node), .gate(register_8_q));
  Transistor #(.\type ("n")) transistor_40 (.in(transistor_79_out), .out(transistor_24_out), .gate(in_3));
  Pull_Resistor #(.pull(1)) pull_resistor_17 (.node(pull_resistor_17_node));
  Transistor #(.\type ("n")) transistor_41 (.in(1'b0), .out(pull_resistor_17_node), .gate(pull_resistor_9_node));
  Pull_Resistor #(.pull(1)) pull_resistor_18 (.node(pull_resistor_18_node));
  Transistor #(.\type ("n")) transistor_42 (.in(1'b0), .out(pull_resistor_18_node), .gate(pull_resistor_10_node));
  Pull_Resistor #(.pull(1)) pull_resistor_19 (.node(pull_resistor_19_node));
  Transistor #(.\type ("n")) transistor_43 (.in(1'b0), .out(pull_resistor_19_node), .gate(transistor_29_out));
  Pull_Resistor #(.pull(1)) pull_resistor_20 (.node(pull_resistor_20_node));
  Transistor #(.\type ("n")) transistor_44 (.in(1'b0), .out(pull_resistor_20_node), .gate(pull_resistor_12_node));
  Pull_Resistor #(.pull(1)) pull_resistor_21 (.node(pull_resistor_21_node));
  Transistor #(.\type ("n")) transistor_45 (.in(1'b0), .out(pull_resistor_21_node), .gate(transistor_33_out));
  Transistor #(.\type ("n")) transistor_46 (.in(1'b0), .out(transistor_46_out), .gate(pull_resistor_14_node));
  Pull_Resistor #(.pull(1)) pull_resistor_22 (.node(transistor_46_out));
  Transistor #(.\type ("n")) transistor_47 (.in(1'b0), .out(transistor_47_out), .gate(pull_resistor_15_node));
  Pull_Resistor #(.pull(1)) pull_resistor_23 (.node(transistor_47_out));
  Transistor #(.\type ("n")) transistor_48 (.in(1'b0), .out(transistor_48_out), .gate(pull_resistor_16_node));
  Pull_Resistor #(.pull(1)) pull_resistor_24 (.node(transistor_48_out));
  Transistor #(.\type ("n")) transistor_49 (.in(1'b1), .out(transistor_49_out), .gate(pull_resistor_9_node));
  Transistor #(.\type ("n")) transistor_50 (.in(1'b0), .out(transistor_49_out), .gate(pull_resistor_17_node));
  Transistor #(.\type ("n")) transistor_51 (.in(1'b1), .out(transistor_51_out), .gate(pull_resistor_17_node));
  Transistor #(.\type ("n")) transistor_52 (.in(1'b0), .out(transistor_51_out), .gate(pull_resistor_9_node));
  Transistor #(.\type ("n")) transistor_53 (.in(1'b1), .out(transistor_53_out), .gate(pull_resistor_10_node));
  Transistor #(.\type ("n")) transistor_54 (.in(1'b0), .out(transistor_53_out), .gate(pull_resistor_18_node));
  Transistor #(.\type ("n")) transistor_55 (.in(1'b1), .out(transistor_55_out), .gate(pull_resistor_18_node));
  Transistor #(.\type ("n")) transistor_56 (.in(1'b0), .out(transistor_55_out), .gate(pull_resistor_10_node));
  Transistor #(.\type ("n")) transistor_57 (.in(1'b1), .out(transistor_57_out), .gate(transistor_29_out));
  Transistor #(.\type ("n")) transistor_58 (.in(1'b0), .out(transistor_57_out), .gate(pull_resistor_19_node));
  Transistor #(.\type ("n")) transistor_59 (.in(1'b1), .out(transistor_59_out), .gate(pull_resistor_19_node));
  Transistor #(.\type ("n")) transistor_60 (.in(1'b0), .out(transistor_59_out), .gate(transistor_29_out));
  Transistor #(.\type ("n")) transistor_61 (.in(1'b1), .out(transistor_61_out), .gate(pull_resistor_12_node));
  Transistor #(.\type ("n")) transistor_62 (.in(1'b0), .out(transistor_61_out), .gate(pull_resistor_20_node));
  Transistor #(.\type ("n")) transistor_63 (.in(1'b1), .out(transistor_63_out), .gate(pull_resistor_20_node));
  Transistor #(.\type ("n")) transistor_64 (.in(1'b0), .out(transistor_63_out), .gate(pull_resistor_12_node));
  Transistor #(.\type ("n")) transistor_65 (.in(1'b1), .out(transistor_65_out), .gate(transistor_33_out));
  Transistor #(.\type ("n")) transistor_66 (.in(1'b0), .out(transistor_65_out), .gate(pull_resistor_21_node));
  Transistor #(.\type ("n")) transistor_67 (.in(1'b1), .out(transistor_67_out), .gate(pull_resistor_21_node));
  Transistor #(.\type ("n")) transistor_68 (.in(1'b0), .out(transistor_67_out), .gate(transistor_33_out));
  Transistor #(.\type ("n")) transistor_69 (.in(1'b1), .out(transistor_69_out), .gate(pull_resistor_14_node));
  Transistor #(.\type ("n")) transistor_70 (.in(1'b0), .out(transistor_69_out), .gate(transistor_46_out));
  Transistor #(.\type ("n")) transistor_71 (.in(1'b1), .out(transistor_71_out), .gate(transistor_46_out));
  Transistor #(.\type ("n")) transistor_72 (.in(1'b0), .out(transistor_71_out), .gate(pull_resistor_14_node));
  Transistor #(.\type ("n")) transistor_73 (.in(1'b1), .out(transistor_73_out), .gate(pull_resistor_15_node));
  Transistor #(.\type ("n")) transistor_74 (.in(1'b0), .out(transistor_73_out), .gate(transistor_47_out));
  Transistor #(.\type ("n")) transistor_75 (.in(1'b1), .out(transistor_75_out), .gate(transistor_47_out));
  Transistor #(.\type ("n")) transistor_76 (.in(1'b0), .out(transistor_75_out), .gate(pull_resistor_15_node));
  Transistor #(.\type ("n")) transistor_77 (.in(1'b1), .out(transistor_77_out), .gate(pull_resistor_16_node));
  Transistor #(.\type ("n")) transistor_78 (.in(1'b0), .out(transistor_77_out), .gate(transistor_48_out));
  Transistor #(.\type ("n")) transistor_79 (.in(1'b1), .out(transistor_79_out), .gate(transistor_48_out));
  Transistor #(.\type ("n")) transistor_80 (.in(1'b0), .out(transistor_79_out), .gate(pull_resistor_16_node));
  Transistor #(.\type ("n")) transistor_81 (.in(1'b1), .out(_268), .gate(transistor_49_out));
  Transistor #(.\type ("n")) transistor_82 (.in(1'b1), .out(_268), .gate(transistor_49_out));
  Transistor #(.\type ("n")) transistor_83 (.in(1'b1), .out(_268_2), .gate(transistor_53_out));
  Transistor #(.\type ("n")) transistor_84 (.in(1'b1), .out(_268_2), .gate(transistor_53_out));
  Transistor #(.\type ("n")) transistor_85 (.in(1'b1), .out(_268_3), .gate(transistor_57_out));
  Transistor #(.\type ("n")) transistor_86 (.in(1'b1), .out(_268_3), .gate(transistor_57_out));
  Transistor #(.\type ("n")) transistor_87 (.in(1'b1), .out(_268_4), .gate(transistor_61_out));
  Transistor #(.\type ("n")) transistor_88 (.in(1'b1), .out(_268_4), .gate(transistor_61_out));
  Transistor #(.\type ("n")) transistor_89 (.in(1'b1), .out(_268_5), .gate(transistor_65_out));
  Transistor #(.\type ("n")) transistor_90 (.in(1'b1), .out(_268_5), .gate(transistor_65_out));
  Transistor #(.\type ("n")) transistor_91 (.in(1'b1), .out(_268_6), .gate(transistor_69_out));
  Transistor #(.\type ("n")) transistor_92 (.in(1'b1), .out(_268_6), .gate(transistor_69_out));
  Transistor #(.\type ("n")) transistor_93 (.in(1'b1), .out(_268_7), .gate(transistor_73_out));
  Transistor #(.\type ("n")) transistor_94 (.in(1'b1), .out(_268_7), .gate(transistor_73_out));
  Transistor #(.\type ("n")) transistor_95 (.in(1'b1), .out(_268_8), .gate(transistor_77_out));
  Transistor #(.\type ("n")) transistor_96 (.in(1'b1), .out(_268_8), .gate(transistor_77_out));
  Transistor #(.\type ("n")) transistor_97 (.in(1'b1), .out(_268), .gate(transistor_49_out));
  Transistor #(.\type ("n")) transistor_98 (.in(1'b1), .out(_268), .gate(transistor_49_out));
  Transistor #(.\type ("n")) transistor_99 (.in(1'b0), .out(_268), .gate(transistor_51_out));
  Transistor #(.\type ("n")) transistor_100 (.in(1'b0), .out(_268), .gate(transistor_51_out));
  Transistor #(.\type ("n")) transistor_101 (.in(1'b1), .out(_268_2), .gate(transistor_53_out));
  Transistor #(.\type ("n")) transistor_102 (.in(1'b1), .out(_268_2), .gate(transistor_53_out));
  Transistor #(.\type ("n")) transistor_103 (.in(1'b0), .out(_268_2), .gate(transistor_55_out));
  Transistor #(.\type ("n")) transistor_104 (.in(1'b0), .out(_268_2), .gate(transistor_55_out));
  Transistor #(.\type ("n")) transistor_105 (.in(1'b1), .out(_268_3), .gate(transistor_57_out));
  Transistor #(.\type ("n")) transistor_106 (.in(1'b1), .out(_268_3), .gate(transistor_57_out));
  Transistor #(.\type ("n")) transistor_107 (.in(1'b0), .out(_268_3), .gate(transistor_59_out));
  Transistor #(.\type ("n")) transistor_108 (.in(1'b0), .out(_268_3), .gate(transistor_59_out));
  Transistor #(.\type ("n")) transistor_109 (.in(1'b1), .out(_268_4), .gate(transistor_61_out));
  Transistor #(.\type ("n")) transistor_110 (.in(1'b1), .out(_268_4), .gate(transistor_61_out));
  Transistor #(.\type ("n")) transistor_111 (.in(1'b0), .out(_268_4), .gate(transistor_63_out));
  Transistor #(.\type ("n")) transistor_112 (.in(1'b0), .out(_268_4), .gate(transistor_63_out));
  Transistor #(.\type ("n")) transistor_113 (.in(1'b1), .out(_268_5), .gate(transistor_65_out));
  Transistor #(.\type ("n")) transistor_114 (.in(1'b1), .out(_268_5), .gate(transistor_65_out));
  Transistor #(.\type ("n")) transistor_115 (.in(1'b0), .out(_268_5), .gate(transistor_67_out));
  Transistor #(.\type ("n")) transistor_116 (.in(1'b0), .out(_268_5), .gate(transistor_67_out));
  Transistor #(.\type ("n")) transistor_117 (.in(1'b1), .out(_268_6), .gate(transistor_69_out));
  Transistor #(.\type ("n")) transistor_118 (.in(1'b1), .out(_268_6), .gate(transistor_69_out));
  Transistor #(.\type ("n")) transistor_119 (.in(1'b0), .out(_268_6), .gate(transistor_71_out));
  Transistor #(.\type ("n")) transistor_120 (.in(1'b0), .out(_268_6), .gate(transistor_71_out));
  Transistor #(.\type ("n")) transistor_121 (.in(1'b1), .out(_268_7), .gate(transistor_73_out));
  Transistor #(.\type ("n")) transistor_122 (.in(1'b1), .out(_268_7), .gate(transistor_73_out));
  Transistor #(.\type ("n")) transistor_123 (.in(1'b0), .out(_268_7), .gate(transistor_75_out));
  Transistor #(.\type ("n")) transistor_124 (.in(1'b0), .out(_268_7), .gate(transistor_75_out));
  Transistor #(.\type ("n")) transistor_125 (.in(1'b1), .out(_268_8), .gate(transistor_77_out));
  Transistor #(.\type ("n")) transistor_126 (.in(1'b1), .out(_268_8), .gate(transistor_77_out));
  Transistor #(.\type ("n")) transistor_127 (.in(1'b0), .out(_268_8), .gate(transistor_79_out));
  Transistor #(.\type ("n")) transistor_128 (.in(1'b0), .out(_268_8), .gate(transistor_79_out));
  Transistor #(.\type ("n")) transistor_129 (.in(1'b1), .out(_268), .gate(transistor_49_out));
  Transistor #(.\type ("n")) transistor_130 (.in(1'b0), .out(_268), .gate(transistor_51_out));
  Transistor #(.\type ("n")) transistor_131 (.in(1'b1), .out(_268_2), .gate(transistor_53_out));
  Transistor #(.\type ("n")) transistor_132 (.in(1'b0), .out(_268_2), .gate(transistor_55_out));
  Transistor #(.\type ("n")) transistor_133 (.in(1'b1), .out(_268_3), .gate(transistor_57_out));
  Transistor #(.\type ("n")) transistor_134 (.in(1'b0), .out(_268_3), .gate(transistor_59_out));
  Transistor #(.\type ("n")) transistor_135 (.in(1'b1), .out(_268_4), .gate(transistor_61_out));
  Transistor #(.\type ("n")) transistor_136 (.in(1'b0), .out(_268_4), .gate(transistor_63_out));
  Transistor #(.\type ("n")) transistor_137 (.in(1'b1), .out(_268_5), .gate(transistor_65_out));
  Transistor #(.\type ("n")) transistor_138 (.in(1'b0), .out(_268_5), .gate(transistor_67_out));
  Transistor #(.\type ("n")) transistor_139 (.in(1'b1), .out(_268_6), .gate(transistor_69_out));
  Transistor #(.\type ("n")) transistor_140 (.in(1'b0), .out(_268_6), .gate(transistor_71_out));
  Transistor #(.\type ("n")) transistor_141 (.in(1'b1), .out(_268_7), .gate(transistor_73_out));
  Transistor #(.\type ("n")) transistor_142 (.in(1'b0), .out(_268_7), .gate(transistor_75_out));
  Transistor #(.\type ("n")) transistor_143 (.in(1'b1), .out(_268_8), .gate(transistor_77_out));
  Transistor #(.\type ("n")) transistor_144 (.in(1'b0), .out(_268_8), .gate(transistor_79_out));

  // Notes on the sheet:
  //   153
  //   153
  //   153
  //   153
  //   153
  //   153
  //   153
  //   153
  //   1096
  //   1660
  //   1096
  //   1660
  //   1096
  //   1660
  //   1096
  //   1660
  //   1096
  //   1660
  //   1096
  //   1660
  //   1096
  //   1660
  //   1096
  //   1660
  //   855
  //   1100
  //   855
  //   1100
  //   855
  //   1100
  //   855
  //   1100
  //   855
  //   1100
  //   855
  //   1100
  //   855
  //   1100
  //   855
  //   1100
endmodule

module Program_Counter_Low_Select_Register (
  input  in_1,
  input  in_2,
  input  in_3,
  input  in_4,
  input  in_5,
  input  in_6,
  input  in_7,
  input  in_8,
  input  in_9,
  input  in_10,
  input  in_11,
  input  in_12,
  input  in_13,
  input  in_14,
  input  in_15,
  input  in_16,
  input  in_17,
  input  in_18,
  output _937,
  output out_20,
  output out_21,
  output out_22,
  output out_23,
  output out_24,
  output out_25,
  output out_26
);

  wire transistor_1_out, transistor_2_out, transistor_3_out, transistor_4_out, transistor_5_out,
       transistor_6_out, transistor_7_out, transistor_8_out;

  Transistor #(.\type ("n")) transistor_1 (.in(in_3), .out(transistor_1_out), .gate(in_1));
  Transistor #(.\type ("n")) transistor_2 (.in(in_5), .out(transistor_2_out), .gate(in_1));
  Transistor #(.\type ("n")) transistor_3 (.in(in_7), .out(transistor_3_out), .gate(in_1));
  Transistor #(.\type ("n")) transistor_4 (.in(in_9), .out(transistor_4_out), .gate(in_1));
  Transistor #(.\type ("n")) transistor_5 (.in(in_11), .out(transistor_5_out), .gate(in_1));
  Transistor #(.\type ("n")) transistor_6 (.in(in_13), .out(transistor_6_out), .gate(in_1));
  Transistor #(.\type ("n")) transistor_7 (.in(in_15), .out(transistor_7_out), .gate(in_1));
  Transistor #(.\type ("n")) transistor_8 (.in(in_17), .out(transistor_8_out), .gate(in_1));
  Transistor #(.\type ("n")) transistor_9 (.in(in_4), .out(transistor_1_out), .gate(in_2));
  Transistor #(.\type ("n")) transistor_10 (.in(in_6), .out(transistor_2_out), .gate(in_2));
  Transistor #(.\type ("n")) transistor_11 (.in(in_8), .out(transistor_3_out), .gate(in_2));
  Transistor #(.\type ("n")) transistor_12 (.in(in_10), .out(transistor_4_out), .gate(in_2));
  Transistor #(.\type ("n")) transistor_13 (.in(in_12), .out(transistor_5_out), .gate(in_2));
  Transistor #(.\type ("n")) transistor_14 (.in(in_14), .out(transistor_6_out), .gate(in_2));
  Transistor #(.\type ("n")) transistor_15 (.in(in_16), .out(transistor_7_out), .gate(in_2));
  Transistor #(.\type ("n")) transistor_16 (.in(in_18), .out(transistor_8_out), .gate(in_2));
  Pull_Resistor #(.pull(1)) pull_resistor_1 (.node(_937));
  Transistor #(.\type ("n")) transistor_17 (.in(1'b0), .out(_937), .gate(transistor_1_out));
  Pull_Resistor #(.pull(1)) pull_resistor_2 (.node(out_20));
  Transistor #(.\type ("n")) transistor_18 (.in(1'b0), .out(out_20), .gate(transistor_2_out));
  Pull_Resistor #(.pull(1)) pull_resistor_3 (.node(out_21));
  Transistor #(.\type ("n")) transistor_19 (.in(1'b0), .out(out_21), .gate(transistor_3_out));
  Transistor #(.\type ("n")) transistor_20 (.in(1'b0), .out(out_22), .gate(transistor_4_out));
  Pull_Resistor #(.pull(1)) pull_resistor_4 (.node(out_22));
  Pull_Resistor #(.pull(1)) pull_resistor_5 (.node(out_23));
  Transistor #(.\type ("n")) transistor_21 (.in(1'b0), .out(out_23), .gate(transistor_5_out));
  Transistor #(.\type ("n")) transistor_22 (.in(1'b0), .out(out_24), .gate(transistor_6_out));
  Pull_Resistor #(.pull(1)) pull_resistor_6 (.node(out_24));
  Pull_Resistor #(.pull(1)) pull_resistor_7 (.node(out_25));
  Transistor #(.\type ("n")) transistor_23 (.in(1'b0), .out(out_25), .gate(transistor_7_out));
  Transistor #(.\type ("n")) transistor_24 (.in(1'b0), .out(out_26), .gate(transistor_8_out));
  Pull_Resistor #(.pull(1)) pull_resistor_8 (.node(out_26));
endmodule

module PCL_Register (
  input  in_1,
  input  in_2,
  input  in_3,
  input  in_4,
  input  in_5,
  output out_6,
  output out_7,
  output out_8
);

  wire pull_resistor_1_node, register_1_q, transistor_1_out, transistor_3_out;

  Transistor #(.\type ("n")) transistor_1 (.in(in_5), .out(transistor_1_out), .gate(in_1));
  Pull_Resistor #(.pull(1)) pull_resistor_1 (.node(pull_resistor_1_node));
  Transistor #(.\type ("n")) transistor_2 (.in(1'b0), .out(pull_resistor_1_node), .gate(register_1_q));
  Register #(.width(1), .trigger("high")) register_1 (
    .D(transistor_1_out), .Q(register_1_q), .clk(in_1));  // open: en, clr
  Transistor #(.\type ("n")) transistor_3 (.in(1'b0), .out(transistor_3_out), .gate(pull_resistor_1_node));
  Pull_Resistor #(.pull(1)) pull_resistor_2 (.node(transistor_3_out));
  Transistor #(.\type ("n")) transistor_4 (.in(transistor_3_out), .out(out_6), .gate(in_4));
  Transistor #(.\type ("n")) transistor_5 (.in(transistor_3_out), .out(out_7), .gate(in_3));
  Transistor #(.\type ("n")) transistor_6 (.in(transistor_3_out), .out(out_8), .gate(in_2));
endmodule
